// Logisim project P0_L0_FSM.circ as structural Verilog: 4 circuits, main circuit fsm
module fsm (
  input  [1:0] In,
  input  CLR,
  output Z
);

  wire clock_1_out;
  wire [2:0] multiplexer_1_out, state_store_1_now_state, state_transform_1_next3;

  Clock clock_1 (.out(clock_1_out));
  state_transform state_transform_1 (
    .in1(In[1]), .in2(In[0]), .now1(state_store_1_now_state[0]), .now2(state_store_1_now_state[1]),
    .now3(state_store_1_now_state[2]), .next1(state_transform_1_next3[2]),
    .next2(state_transform_1_next3[1]), .next3(state_transform_1_next3[0]));
  state_store state_store_1 (
    .input_state(multiplexer_1_out), .clk(clock_1_out), .reset(1'b0), .now_state(state_store_1_now_state));
  Multiplexer #(.width(3)) multiplexer_1 (
    .in0(state_transform_1_next3), .in1(3'b000), .out(multiplexer_1_out), .sel(CLR));  // open: en
  \output  output_1 (
    .state1(state_store_1_now_state[0]), .state2(state_store_1_now_state[1]),
    .state3(state_store_1_now_state[2]), .in1(In[1]), .in2(In[0]), .out(Z));
endmodule

module state_transform (
  input  in1,
  input  in2,
  input  now1,
  input  now2,
  input  now3,
  output next1,
  output next2,
  output next3
);

  wire and_1_out, and_2_out, and_3_out, and_4_out, and_5_out, and_6_out, and_7_out, and_8_out, and_9_out,
       and_10_out, not_1_out, not_2_out, not_3_out, not_4_out, not_5_out, not_6_out, not_7_out, not_8_out,
       not_9_out, not_10_out, not_11_out, not_12_out, not_13_out, not_14_out, not_15_out, not_16_out,
       not_17_out, not_18_out, not_19_out, not_20_out, not_21_out, not_22_out, not_23_out, not_24_out;

  not not_1 (not_1_out, in1);
  not not_2 (not_2_out, now2);
  not not_3 (not_3_out, now3);
  not not_4 (not_4_out, in2);
  not not_5 (not_5_out, now2);
  not not_6 (not_6_out, in1);
  not not_7 (not_7_out, now1);
  not not_8 (not_8_out, now2);
  not not_9 (not_9_out, in2);
  not not_10 (not_10_out, now2);
  not not_11 (not_11_out, in2);
  not not_12 (not_12_out, now1);
  not not_13 (not_13_out, now3);
  not not_14 (not_14_out, in2);
  not not_15 (not_15_out, now1);
  not not_16 (not_16_out, now3);
  not not_17 (not_17_out, in2);
  not not_18 (not_18_out, now2);
  not not_19 (not_19_out, now3);
  not not_20 (not_20_out, in1);
  not not_21 (not_21_out, now1);
  not not_22 (not_22_out, now3);
  not not_23 (not_23_out, in1);
  not not_24 (not_24_out, in1);
  and and_1 (and_1_out, not_1_out, now1, not_2_out, not_3_out);
  and and_2 (and_2_out, not_4_out, now1, not_5_out);
  and and_3 (and_3_out, not_6_out, in2, not_7_out, not_8_out, now3);
  and and_4 (and_4_out, not_9_out, not_10_out, now3);
  and and_5 (and_5_out, not_11_out, not_12_out, now2, not_13_out);
  and and_6 (and_6_out, not_14_out, not_15_out, now2, not_16_out);
  and and_7 (and_7_out, not_17_out, now1, not_18_out, not_19_out);
  and and_8 (and_8_out, not_20_out, in2, not_21_out, not_22_out);
  and and_9 (and_9_out, not_23_out, in2, now2);
  and and_10 (and_10_out, not_24_out, in2, now1, now3);
  or or_1 (next1, and_1_out, and_2_out, and_3_out);
  or or_2 (next2, and_4_out, and_5_out);
  or or_3 (next3, and_6_out, and_7_out, and_8_out, and_9_out, and_10_out);
endmodule

module state_store (
  input  [2:0] input_state,
  input  reset,
  input  clk,
  output [2:0] now_state
);

  Register #(.width(3)) register_1 (.D(input_state), .en(1'b1), .Q(now_state), .clk(clk), .clr(reset));
endmodule

module \output  (
  input  state1,
  input  state2,
  input  state3,
  input  in1,
  input  in2,
  output out
);

  wire and_1_out, and_2_out, not_1_out, not_2_out, not_3_out, not_4_out, not_5_out;

  not not_1 (not_1_out, state1);
  not not_2 (not_2_out, state3);
  not not_3 (not_3_out, in2);
  not not_4 (not_4_out, state2);
  not not_5 (not_5_out, in2);
  and and_1 (and_1_out, not_1_out, state2, not_2_out, not_3_out);
  and and_2 (and_2_out, state1, not_4_out, state3, not_5_out);
  or or_1 (out, and_1_out, and_2_out);
endmodule
