// Logisim project 1-period-CPU-jal.circ as structural Verilog: 12 circuits, main circuit main
module main (
  input  in_1,
  output [31:0] Instr,
  output RegWrite,
  output [4:0] RegAddr,
  output [31:0] RegData,
  output [4:0] MemAddr,
  output MemWrite,
  output [31:0] MemData
);

  wire ALU_BSel, Zero;
  wire [1:0] ALUOp, EXTOp, GRF_A3Sel, GRF_WDSel, NPCOp;
  wire [31:0] ALU_C, DM_RD, Ext, GRF_RD1, multiplexer_1_out, NPC, PC, PC_Do8;

  Multiplexer #(.width(32)) multiplexer_1 (
    .in0(MemData), .in1(Ext), .out(multiplexer_1_out), .sel(ALU_BSel));  // open: en
  PC pc_1 (.Di(NPC), .Reset(in_1), .Do(PC));
  NPC npc_1 (.IMM(Instr[25:0]), .PC(PC), .NPC(NPC), .NPCOp(NPCOp), .Zero(Zero), .PC_Do8(PC_Do8));
  ALU alu_1 (.ALUOp(ALUOp), .A(GRF_RD1), .B(multiplexer_1_out), .C({ALU_C[31:7], MemAddr, ALU_C[1:0]}), .Zero(Zero));
  IM im_1 (.A(PC), .D(Instr));
  Multiplexer #(.select(2), .width(5)) multiplexer_2 (
    .in0(Instr[15:11]), .in1(Instr[20:16]), .in2({5{1'b1}}), .out(RegAddr), .sel(GRF_A3Sel));  // open: in3, en
  DM dm_1 (.A({ALU_C[31:7], MemAddr, ALU_C[1:0]}), .RD(DM_RD), .reset(in_1), .DMWr(MemWrite), .WD(MemData));
  EXT ext_1 (.Imm(Instr[15:0]), .EXTOp(EXTOp), .Ext(Ext));
  Controller controller (
    .opcode(Instr[31:26]), .funct(Instr[5:0]), .ALUOp(ALUOp), .GRF_WDSel(GRF_WDSel), .EXTOp(EXTOp),
    .NPCOp(NPCOp), .RFWr(RegWrite), .DMWr(MemWrite), .GRF_A3Sel(GRF_A3Sel), .ALU_BSel(ALU_BSel));
  GRF grf_1 (
    .reset(in_1), .WE(RegWrite), .A1(Instr[25:21]), .A2(Instr[20:16]), .A3(RegAddr), .WD(RegData),
    .RD1(GRF_RD1), .RD2(MemData));
  Multiplexer #(.select(2), .width(32)) multiplexer_3 (
    .in0({ALU_C[31:7], MemAddr, ALU_C[1:0]}), .in1(DM_RD), .in2(Ext), .in3(PC_Do8), .out(RegData),
    .sel(GRF_WDSel));  // open: en

  // Other names for the same wires on the sheet: ALU_C[6:2] = MemAddr; DMWr = MemWrite; GRF_A3[4:0] = RegAddr;
  //   GRF_RD2[31:0] = MemData; GRF_WD[31:0] = RegData; opcode[5:0] = Instr[31:26]; EXT_Imm[15:0] = Instr[15:0];
  //   funct[5:0] = Instr[5:0]; NPC_IMM[25:0] = Instr[25:0]; GRF_A2[4:0] = Instr[20:16]; GRF_A1[4:0] = Instr[25:21];
  //   reset = in_1; RFWr = RegWrite
endmodule

module GRF (
  input  reset,
  input  WE,
  input  [4:0] A1,
  input  [4:0] A2,
  input  [4:0] A3,
  input  [31:0] WD,
  output [31:0] RD1,
  output [31:0] RD2
);

  wire clk, demultiplexer_1_out1, demultiplexer_1_out2, demultiplexer_1_out3, demultiplexer_1_out4,
       demultiplexer_1_out5, demultiplexer_1_out6, demultiplexer_1_out7, demultiplexer_1_out8,
       demultiplexer_1_out9, demultiplexer_1_out10, demultiplexer_1_out11, demultiplexer_1_out12,
       demultiplexer_1_out13, demultiplexer_1_out14, demultiplexer_1_out15, demultiplexer_1_out16,
       demultiplexer_1_out17, demultiplexer_1_out18, demultiplexer_1_out19, demultiplexer_1_out20,
       demultiplexer_1_out21, demultiplexer_1_out22, demultiplexer_1_out23, demultiplexer_1_out24,
       demultiplexer_1_out25, demultiplexer_1_out26, demultiplexer_1_out27, demultiplexer_1_out28,
       demultiplexer_1_out29, demultiplexer_1_out30, demultiplexer_1_out31;
  wire [31:0] GR1_q, GR2_q, GR3_q, GR4_q, GR5_q, GR6_q, GR7_q, GR8_q, GR9_q, GR10_q, GR11_q, GR12_q, GR13_q,
       GR14_q, GR15_q, GR16_q, GR17_q, GR18_q, GR19_q, GR20_q, GR21_q, GR22_q, GR23_q, GR24_q, GR25_q,
       GR26_q, GR27_q, GR28_q, GR29_q, GR30_q, GR31_q, GR32_q;

  Demultiplexer #(.select(5)) demultiplexer_1 (
    .out1(demultiplexer_1_out1), .out2(demultiplexer_1_out2), .out3(demultiplexer_1_out3),
    .out4(demultiplexer_1_out4), .out5(demultiplexer_1_out5), .out6(demultiplexer_1_out6),
    .out7(demultiplexer_1_out7), .out8(demultiplexer_1_out8), .out9(demultiplexer_1_out9),
    .out10(demultiplexer_1_out10), .out11(demultiplexer_1_out11), .out12(demultiplexer_1_out12),
    .out13(demultiplexer_1_out13), .out14(demultiplexer_1_out14), .out15(demultiplexer_1_out15),
    .out16(demultiplexer_1_out16), .out17(demultiplexer_1_out17), .out18(demultiplexer_1_out18),
    .out19(demultiplexer_1_out19), .out20(demultiplexer_1_out20), .out21(demultiplexer_1_out21),
    .out22(demultiplexer_1_out22), .out23(demultiplexer_1_out23), .out24(demultiplexer_1_out24),
    .out25(demultiplexer_1_out25), .out26(demultiplexer_1_out26), .out27(demultiplexer_1_out27),
    .out28(demultiplexer_1_out28), .out29(demultiplexer_1_out29), .out30(demultiplexer_1_out30),
    .out31(demultiplexer_1_out31), .in(WE), .sel(A3), .en(1'b1));  // open: out0
  Clock clock_1 (.out(clk));
  Register #(.width(32)) GR1 (.D({32{1'b0}}), .Q(GR1_q), .clk(clk), .clr(reset));  // open: en
  Register #(.width(32)) GR2 (.D(WD), .en(demultiplexer_1_out1), .Q(GR2_q), .clk(clk), .clr(reset));
  Register #(.width(32)) GR3 (.D(WD), .en(demultiplexer_1_out2), .Q(GR3_q), .clk(clk), .clr(reset));
  Register #(.width(32)) GR4 (.D(WD), .en(demultiplexer_1_out3), .Q(GR4_q), .clk(clk), .clr(reset));
  Register #(.width(32)) GR5 (.D(WD), .en(demultiplexer_1_out4), .Q(GR5_q), .clk(clk), .clr(reset));
  Register #(.width(32)) GR6 (.D(WD), .en(demultiplexer_1_out5), .Q(GR6_q), .clk(clk), .clr(reset));
  Register #(.width(32)) GR7 (.D(WD), .en(demultiplexer_1_out6), .Q(GR7_q), .clk(clk), .clr(reset));
  Register #(.width(32)) GR8 (.D(WD), .en(demultiplexer_1_out7), .Q(GR8_q), .clk(clk), .clr(reset));
  Register #(.width(32)) GR9 (.D(WD), .en(demultiplexer_1_out8), .Q(GR9_q), .clk(clk), .clr(reset));
  Register #(.width(32)) GR10 (.D(WD), .en(demultiplexer_1_out9), .Q(GR10_q), .clk(clk), .clr(reset));
  Register #(.width(32)) GR11 (.D(WD), .en(demultiplexer_1_out10), .Q(GR11_q), .clk(clk), .clr(reset));
  Register #(.width(32)) GR12 (.D(WD), .en(demultiplexer_1_out11), .Q(GR12_q), .clk(clk), .clr(reset));
  Register #(.width(32)) GR13 (.D(WD), .en(demultiplexer_1_out12), .Q(GR13_q), .clk(clk), .clr(reset));
  Register #(.width(32)) GR14 (.D(WD), .en(demultiplexer_1_out13), .Q(GR14_q), .clk(clk), .clr(reset));
  Register #(.width(32)) GR15 (.D(WD), .en(demultiplexer_1_out14), .Q(GR15_q), .clk(clk), .clr(reset));
  Register #(.width(32)) GR16 (.D(WD), .en(demultiplexer_1_out15), .Q(GR16_q), .clk(clk), .clr(reset));
  Register #(.width(32)) GR17 (.D(WD), .en(demultiplexer_1_out16), .Q(GR17_q), .clk(clk), .clr(reset));
  Register #(.width(32)) GR18 (.D(WD), .en(demultiplexer_1_out17), .Q(GR18_q), .clk(clk), .clr(reset));
  Register #(.width(32)) GR19 (.D(WD), .en(demultiplexer_1_out18), .Q(GR19_q), .clk(clk), .clr(reset));
  Register #(.width(32)) GR20 (.D(WD), .en(demultiplexer_1_out19), .Q(GR20_q), .clk(clk), .clr(reset));
  Register #(.width(32)) GR21 (.D(WD), .en(demultiplexer_1_out20), .Q(GR21_q), .clk(clk), .clr(reset));
  Register #(.width(32)) GR22 (.D(WD), .en(demultiplexer_1_out21), .Q(GR22_q), .clk(clk), .clr(reset));
  Register #(.width(32)) GR23 (.D(WD), .en(demultiplexer_1_out22), .Q(GR23_q), .clk(clk), .clr(reset));
  Register #(.width(32)) GR24 (.D(WD), .en(demultiplexer_1_out23), .Q(GR24_q), .clk(clk), .clr(reset));
  Register #(.width(32)) GR25 (.D(WD), .en(demultiplexer_1_out24), .Q(GR25_q), .clk(clk), .clr(reset));
  Register #(.width(32)) GR26 (.D(WD), .en(demultiplexer_1_out25), .Q(GR26_q), .clk(clk), .clr(reset));
  Register #(.width(32)) GR27 (.D(WD), .en(demultiplexer_1_out26), .Q(GR27_q), .clk(clk), .clr(reset));
  Register #(.width(32)) GR28 (.D(WD), .en(demultiplexer_1_out27), .Q(GR28_q), .clk(clk), .clr(reset));
  Register #(.width(32)) GR29 (.D(WD), .en(demultiplexer_1_out28), .Q(GR29_q), .clk(clk), .clr(reset));
  Register #(.width(32)) GR30 (.D(WD), .en(demultiplexer_1_out29), .Q(GR30_q), .clk(clk), .clr(reset));
  Register #(.width(32)) GR31 (.D(WD), .en(demultiplexer_1_out30), .Q(GR31_q), .clk(clk), .clr(reset));
  Register #(.width(32)) GR32 (.D(WD), .en(demultiplexer_1_out31), .Q(GR32_q), .clk(clk), .clr(reset));
  Multiplexer #(.select(5), .width(32)) multiplexer_1 (
    .in0(GR1_q), .in1(GR2_q), .in2(GR3_q), .in3(GR4_q), .in4(GR5_q), .in5(GR6_q), .in6(GR7_q), .in7(GR8_q),
    .in8(GR9_q), .in9(GR10_q), .in10(GR11_q), .in11(GR12_q), .in12(GR13_q), .in13(GR14_q), .in14(GR15_q),
    .in15(GR16_q), .in16(GR17_q), .in17(GR18_q), .in18(GR19_q), .in19(GR20_q), .in20(GR21_q), .in21(GR22_q),
    .in22(GR23_q), .in23(GR24_q), .in24(GR25_q), .in25(GR26_q), .in26(GR27_q), .in27(GR28_q), .in28(GR29_q),
    .in29(GR30_q), .in30(GR31_q), .in31(GR32_q), .out(RD1), .sel(A1), .en(1'b1));
  // Probe on A1
  // Probe on A2
  Multiplexer #(.select(5), .width(32)) multiplexer_2 (
    .in0(GR1_q), .in1(GR2_q), .in2(GR3_q), .in3(GR4_q), .in4(GR5_q), .in5(GR6_q), .in6(GR7_q), .in7(GR8_q),
    .in8(GR9_q), .in9(GR10_q), .in10(GR11_q), .in11(GR12_q), .in12(GR13_q), .in13(GR14_q), .in14(GR15_q),
    .in15(GR16_q), .in16(GR17_q), .in17(GR18_q), .in18(GR19_q), .in19(GR20_q), .in20(GR21_q), .in21(GR22_q),
    .in22(GR23_q), .in23(GR24_q), .in24(GR25_q), .in25(GR26_q), .in26(GR27_q), .in27(GR28_q), .in28(GR29_q),
    .in29(GR30_q), .in30(GR31_q), .in31(GR32_q), .out(RD2), .sel(A2), .en(1'b1));
endmodule

module PC (
  input  [31:0] Di,
  input  Reset,
  output [31:0] Do
);

  wire clock_1_out;

  Register #(.width(32)) register_1 (.D(Di), .Q(Do), .clk(clock_1_out), .clr(Reset));  // open: en
  Clock clock_1 (.out(clock_1_out));
endmodule

module NPC (
  input  [31:0] PC,
  input  [25:0] IMM,
  input  Zero,
  input  [1:0] NPCOp,
  output [31:0] NPC,
  output [31:0] PC_Do8
);

  wire and_1_out, and_2_out, not_1_out, not_2_out;
  wire [1:0] multiplexer_1_out;
  wire [31:0] adder_1_out, adder_2_out, bit_extender_1_out, subtractor_1_out;

  assign bit_extender_1_out = {{14{IMM[15]}}, {IMM[15:0], 2'b00}};  // Bit_Extender bit_extender_1
  Adder #(.width(32)) adder_1 (.a(bit_extender_1_out), .b(adder_2_out), .out(adder_1_out));  // open: cin, cout
  Adder #(.width(32)) adder_2 (.a(PC), .b(32'h4), .out(adder_2_out));  // open: cin, cout
  Subtractor #(.width(32)) subtractor_1 (
    .a({PC[31:28], IMM, 2'b00}), .b(32'h3000), .out(subtractor_1_out));  // open: bin, bout
  Adder #(.width(32)) adder_3 (.a(adder_2_out), .b(32'h3000), .out(PC_Do8));  // open: cin, cout
  Multiplexer #(.width(2)) multiplexer_1 (
    .in0(NPCOp), .in1(2'b00), .out(multiplexer_1_out), .sel(and_1_out));  // open: en
  Multiplexer #(.select(2), .width(32)) multiplexer_2 (
    .in0(adder_2_out), .in1(adder_1_out), .in2(subtractor_1_out), .out(NPC), .sel(multiplexer_1_out),
    .en(1'b1));  // open: in3
  and and_1 (and_1_out, and_2_out, not_1_out);
  and and_2 (and_2_out, not_2_out, NPCOp[0]);
  not not_1 (not_1_out, Zero);
  not not_2 (not_2_out, NPCOp[1]);
endmodule

module EXT (
  input  [15:0] Imm,
  input  [1:0] EXTOp,
  output [31:0] Ext
);

  wire [31:0] bit_extender_1_out, bit_extender_2_out;

  assign bit_extender_1_out = {{16{1'b0}}, Imm};  // Bit_Extender bit_extender_1
  assign bit_extender_2_out = {{16{Imm[15]}}, Imm};  // Bit_Extender bit_extender_2
  Multiplexer #(.select(2), .width(32)) multiplexer_1 (
    .in0(bit_extender_1_out), .in1(bit_extender_2_out), .in2({Imm, {16{1'b0}}}), .out(Ext), .sel(EXTOp));  // open: in3, en
endmodule

module IM (
  input  [31:0] A,
  output [31:0] D
);

  ROM #(.addrWidth(5), .dataWidth(32)) rom_1 (.addr(A[6:2]), .data(D), .sel(1'b1));

  // Notes on the sheet:
  //   contents of rom_1 (hex, n*v repeats v):
  //   3c12ffff 36528901 3c1198d8 363192ab 2519823 3c108324 3610a987 2127821 c000c09 2707023 3f26821
  //   c000c0c 3f0a021
endmodule

module DM (
  input  [31:0] A,
  input  reset,
  input  [31:0] WD,
  input  DMWr,
  output [31:0] RD
);

  wire clock_1_out;

  Clock clock_1 (.out(clock_1_out));
  RAM #(.addrWidth(5), .dataWidth(32), .bus("separate")) ram_1 (
    .addr(A[6:2]), .din(WD), .data(RD), .str(DMWr), .clk(clock_1_out), .ld(1'b1), .clr(reset));  // open: sel
endmodule

module ALU (
  input  [1:0] ALUOp,
  input  [31:0] A,
  input  [31:0] B,
  output [31:0] C,
  output Zero
);

  wire alucontroller_1_cin, alucontroller_1_grf_a3sel, alucontroller_1_grf_wdsel;
  wire [31:0] adder_1_out, multiplexer_1_out, not_1_out, or_1_out;

  assign or_1_out = B | A;  // OR_Gate or_1, 32 bits wide
  ALUController alucontroller_1 (
    .ALUOp(ALUOp), .GRF_A3Sel(alucontroller_1_grf_a3sel), .Cin(alucontroller_1_cin),
    .GRF_WDSel(alucontroller_1_grf_wdsel));  // open: SExt
  assign not_1_out = ~B;  // NOT_Gate not_1, 32 bits wide
  Multiplexer #(.width(32)) multiplexer_1 (
    .in0(B), .in1(not_1_out), .out(multiplexer_1_out), .sel(alucontroller_1_grf_a3sel));  // open: en
  Adder #(.width(32)) adder_1 (
    .a(A), .b(multiplexer_1_out), .out(adder_1_out), .cin(alucontroller_1_cin));  // open: cout
  Comparator #(.width(32)) comparator_1 (.a(adder_1_out), .b({32{1'b0}}), .eq(Zero));  // open: gt, lt
  Multiplexer #(.width(32)) multiplexer_2 (
    .in0(adder_1_out), .in1(or_1_out), .out(C), .sel(alucontroller_1_grf_wdsel));  // open: en
endmodule

// controller
module Controller (
  input  [5:0] opcode,
  input  [5:0] funct,
  output [1:0] ALUOp,
  output [1:0] GRF_WDSel,
  output [1:0] EXTOp,
  output ALU_BSel,
  output DMWr,
  output RFWr,
  output [1:0] GRF_A3Sel,
  output [1:0] NPCOp
);

  wire addi, addu, addu_out, Beq, jal, lui, lw, not_1_out, not_2_out, not_3_out, not_4_out, not_5_out,
       not_6_out, not_7_out, not_8_out, not_9_out, not_10_out, not_11_out, not_12_out, not_13_out,
       not_14_out, not_15_out, not_16_out, not_17_out, not_18_out, not_19_out, not_20_out, not_21_out,
       not_22_out, not_23_out, not_24_out, not_25_out, not_26_out, not_27_out, not_28_out, not_29_out,
       not_30_out, not_31_out, not_32_out, not_33_out, not_34_out, not_35_out, not_36_out, not_37_out, Ori,
       R, subu, subu_out, sw;

  not not_1 (not_1_out, opcode[0]);
  not not_2 (not_2_out, opcode[5]);
  not not_3 (not_3_out, opcode[1]);
  not not_4 (not_4_out, opcode[2]);
  not not_5 (not_5_out, opcode[4]);
  not not_6 (not_6_out, opcode[3]);
  and u_R (R, not_1_out, not_3_out, not_4_out, not_6_out, not_5_out, not_2_out);
  not not_7 (not_7_out, funct[4]);
  not not_8 (not_8_out, funct[3]);
  not not_9 (not_9_out, funct[2]);
  not not_10 (not_10_out, funct[1]);
  and u_addu (addu_out, funct[0], not_10_out, not_9_out, not_8_out, not_7_out, funct[5]);
  and and_1 (addu, addu_out, R);
  not not_11 (not_11_out, opcode[0]);
  not not_12 (not_12_out, opcode[1]);
  and u_Beq (Beq, not_11_out, not_12_out, opcode[2], not_13_out, not_14_out, not_15_out);
  not not_13 (not_13_out, opcode[3]);
  not not_14 (not_14_out, opcode[4]);
  not not_15 (not_15_out, opcode[5]);
  not not_16 (not_16_out, funct[2]);
  not not_17 (not_17_out, funct[4]);
  not not_18 (not_18_out, funct[3]);
  and u_subu (subu_out, funct[0], funct[1], not_16_out, not_18_out, not_17_out, funct[5]);
  and and_2 (subu, subu_out, R);
  not not_19 (not_19_out, opcode[4]);
  not not_20 (not_20_out, opcode[1]);
  not not_21 (not_21_out, opcode[5]);
  and u_Ori (Ori, opcode[0], not_20_out, opcode[2], opcode[3], not_19_out, not_21_out);
  not not_22 (not_22_out, opcode[2]);
  and u_lw (lw, opcode[0], opcode[1], not_22_out, not_24_out, not_23_out, opcode[5]);
  or_logic or_logic_1 (
    .addu(addu), .subu(subu), .ori(Ori), .lw(lw), .sw(sw), .beq(Beq), .lui(lui), .jal(jal),
    .NPCOp1(NPCOp[1]), .NPCOp2(NPCOp[0]), .RFWr(RFWr), .EXTOp1(EXTOp[1]), .EXTOp2(EXTOp[0]),
    .ALUOp1(ALUOp[1]), .ALUOp2(ALUOp[0]), .DMWr(DMWr), .GRF_A3Sel1(GRF_A3Sel[1]), .GRF_A3Sel2(GRF_A3Sel[0]),
    .GRF_WDSel1(GRF_WDSel[1]), .GRF_WDSel2(GRF_WDSel[0]), .ALU_BSel(ALU_BSel));
  not not_23 (not_23_out, opcode[4]);
  not not_24 (not_24_out, opcode[3]);
  not not_25 (not_25_out, opcode[4]);
  not not_26 (not_26_out, opcode[2]);
  and u_sw (sw, opcode[0], opcode[1], not_26_out, opcode[3], not_25_out, opcode[5]);
  and u_lui (lui, opcode[0], opcode[1], opcode[2], opcode[3], not_27_out, not_28_out);
  not not_27 (not_27_out, opcode[4]);
  not not_28 (not_28_out, opcode[5]);
  not not_29 (not_29_out, opcode[0]);
  not not_30 (not_30_out, opcode[2]);
  not not_31 (not_31_out, opcode[1]);
  not not_32 (not_32_out, opcode[5]);
  not not_33 (not_33_out, opcode[4]);
  and u_Addi (addi, not_29_out, not_31_out, not_30_out, opcode[3], not_33_out, not_32_out);
  not not_34 (not_34_out, opcode[2]);
  and u_jal (jal, opcode[0], opcode[1], not_34_out, not_36_out, not_35_out, not_37_out);
  not not_35 (not_35_out, opcode[4]);
  not not_36 (not_36_out, opcode[3]);
  not not_37 (not_37_out, opcode[5]);
endmodule

module ALUController (
  input  [1:0] ALUOp,
  output SExt,
  output GRF_A3Sel,
  output Cin,
  output GRF_WDSel
);

  wire not_2_out, not_3_out;

  not not_1 (SExt, ALUOp[1]);
  not not_2 (not_2_out, ALUOp[1]);
  not not_3 (not_3_out, ALUOp[1]);
  and and_1 (GRF_WDSel, ALUOp[0], ALUOp[1]);
  and and_2 (GRF_A3Sel, ALUOp[0], not_2_out);
  and and_3 (Cin, ALUOp[0], not_3_out);
endmodule

module or_logic (
  input  addu,
  input  subu,
  input  ori,
  input  lw,
  input  sw,
  input  beq,
  input  lui,
  input  jal,
  output NPCOp1,
  output NPCOp2,
  output RFWr,
  output EXTOp1,
  output EXTOp2,
  output ALUOp1,
  output ALUOp2,
  output DMWr,
  output GRF_A3Sel1,
  output GRF_A3Sel2,
  output GRF_WDSel1,
  output GRF_WDSel2,
  output ALU_BSel
);

  buf or_1 (NPCOp1, jal);  // OR_Gate
  buf or_2 (NPCOp2, beq);  // OR_Gate
  or or_3 (RFWr, addu, subu, ori, lw, lui, jal);
  buf or_4 (EXTOp1, lui);  // OR_Gate
  or or_5 (EXTOp2, lw, sw);
  buf or_6 (ALUOp1, ori);  // OR_Gate
  or or_7 (ALUOp2, subu, ori, beq);
  buf or_8 (DMWr, sw);  // OR_Gate
  buf or_9 (GRF_A3Sel1, jal);  // OR_Gate
  or or_10 (GRF_A3Sel2, ori, lw, lui);
  or or_11 (GRF_WDSel1, lui, jal);
  or or_12 (GRF_WDSel2, lw, jal);
  or or_13 (ALU_BSel, sw, ori, lw);
endmodule

module test (
  input  reset
);

  wire main_1_memwrite, main_1_regwrite;
  wire [4:0] main_1_memaddr, main_1_regaddr;
  wire [31:0] main_1_instr, main_1_memdata, main_1_regdata;

  main main_1 (
    .in_1(reset), .Instr(main_1_instr), .RegWrite(main_1_regwrite), .RegAddr(main_1_regaddr),
    .RegData(main_1_regdata), .MemAddr(main_1_memaddr), .MemWrite(main_1_memwrite), .MemData(main_1_memdata));
  // Probe on main_1_instr
  // Probe on main_1_regwrite
  // Probe on main_1_regaddr
  // Probe on main_1_memwrite
  // Probe on main_1_memdata
  // Probe on main_1_regdata
  // Probe on main_1_memaddr
endmodule
