// Logisim project pipeline-CPU-backup.circ as structural Verilog: 17 circuits, main circuit main
module main (
  input  reset,
  output [31:0] pc_m,
  output RegWrite,
  output [4:0] RegAddr,
  output [31:0] RegData,
  output [31:0] pc_w,
  output MemWrite,
  output [31:0] MemAddr,
  output [31:0] MemData
);

  wire alu_1_zero, and_1_out, controller_1_alusrcd, controller_1_branchd, controller_1_jald,
       controller_1_memtoregd, controller_1_memwrited, controller_1_regwrited, e_register_1_alusrce,
       e_register_1_branche, e_register_1_memtorege, e_register_1_memwritee, e_register_1_regwritee,
       e_register_1_regwritee_2, JalW, m_register_1_branchm, m_register_1_jalm, m_register_1_memtoregm,
       m_register_1_regwritem, m_register_1_zerom, w_register_1_memtoregw;
  wire [1:0] controller_1_alucontrol, controller_1_extop, controller_1_jumpd, controller_1_regdstd,
       e_register_1_alucontrole, e_register_1_regdste;
  wire [3:0] adder_1_out_2;
  wire [4:0] e_register_1_rde_2, e_register_1_rte_2, m_register_1_writeregm4_0, multiplexer_5_out,
       w_register_1_writeregw4_0;
  wire [27:0] adder_1_out, sll2_1_out_2;
  wire [31:0] adder_2_out, adder_3_out, alu_1_c, dm_1_rd, e_register_1_pcplus4e, e_register_1_rd1out,
       e_register_1_rd2out, e_register_1_signimme, ext_1_ext, grf_1_rd1, grf_1_rd2, im_1_d, jal_instrd,
       jal_pc_d, jal_pcplus4d, m_register_1_pcbranchm, multiplexer_1_out, multiplexer_2_out,
       multiplexer_6_out, multiplexer_7_out, pc_1_do, pc_e, pc_m_t, pc_w_t, sll2_2_out_2,
       w_register_1_aluoutw, w_register_1_readdatam;
  wire [31:28] sll2_1_out_2_2;

  assign pc_w = pc_w_t | 32'h3000;  // OR_Gate or_1, 32 bits wide
  Multiplexer #(.width(32)) multiplexer_1 (
    .in0({adder_1_out_2, adder_1_out}), .in1(m_register_1_pcbranchm), .out(multiplexer_1_out), .sel(and_1_out));  // open: en
  Multiplexer #(.select(2), .width(32)) multiplexer_2 (
    .in0(multiplexer_1_out), .in1({adder_1_out_2, sll2_1_out_2}), .in2(grf_1_rd1), .out(multiplexer_2_out),
    .sel(controller_1_jumpd));  // open: in3, en
  // Probe on pc_1_do
  PC pc_1 (.Di(multiplexer_2_out), .Do(pc_1_do), .Reset(reset));
  assign pc_m = pc_m_t | 32'h3000;  // OR_Gate or_2, 32 bits wide
  // Probe on jal_instrd
  D_register jal (
    .PC_W(pc_1_do), .IM_D(im_1_d), .PCPlus4F({adder_1_out_2, adder_1_out}), .PC_D(jal_pc_d),
    .InstrD(jal_instrd), .PCPlus4D(jal_pcplus4d), .reset(reset));
  Adder #(.width(32)) adder_1 (.a(pc_1_do), .b(32'h4), .out({adder_1_out_2, adder_1_out}));  // open: cin, cout
  IM im_1 (.A(pc_1_do), .D(im_1_d));
  Multiplexer #(.width(32)) multiplexer_3 (
    .in0(multiplexer_7_out), .in1(adder_2_out), .out(RegData), .sel(JalW));  // open: en
  Adder #(.width(32)) adder_2 (.a(pc_w_t), .b(32'h8), .out(adder_2_out));  // open: cin, cout
  Controller controller_1 (
    .opcode(jal_instrd[31:26]), .funct(jal_instrd[5:0]), .BranchD(controller_1_branchd),
    .JalD(controller_1_jald), .RegWriteD(controller_1_regwrited), .EXTOp(controller_1_extop),
    .ALUControl(controller_1_alucontrol), .MemWriteD(controller_1_memwrited), .RegDstD(controller_1_regdstd),
    .JumpD(controller_1_jumpd), .MemtoRegD(controller_1_memtoregd), .ALUSrcD(controller_1_alusrcd));
  sll2 sll2_1 (.in_1(jal_instrd), .out_2({sll2_1_out_2_2, sll2_1_out_2}));
  Multiplexer #(.width(5)) multiplexer_4 (
    .in0(w_register_1_writeregw4_0), .in1({5{1'b1}}), .out(RegAddr), .sel(JalW));  // open: en
  GRF grf_1 (
    .reset(reset), .WE(RegWrite), .A1(jal_instrd[25:21]), .A2(jal_instrd[20:16]), .A3(RegAddr), .WD(RegData),
    .RD1(grf_1_rd1), .RD2(grf_1_rd2));
  E_register e_register_1 (
    .RegWriteD(controller_1_regwrited), .MemtoRegD(controller_1_memtoregd),
    .MemWriteD(controller_1_memwrited), .BranchD(controller_1_branchd),
    .ALUControlD(controller_1_alucontrol), .ALUSrcD(controller_1_alusrcd), .RegDstD(controller_1_regdstd),
    .PC_D(jal_pc_d), .RD1(grf_1_rd1), .RD2(grf_1_rd2), .rtE(jal_instrd[20:16]), .rdE(jal_instrd[15:11]),
    .Signext(ext_1_ext), .PCPlus4D(jal_pcplus4d), .RegWriteE_2(e_register_1_regwritee_2),
    .MemtoRegE(e_register_1_memtorege), .MemWriteE(e_register_1_memwritee), .BranchE(e_register_1_branche),
    .ALUControlE(e_register_1_alucontrole), .ALUSrcE(e_register_1_alusrce), .RegDstE(e_register_1_regdste),
    .PC_E(pc_e), .RD1out(e_register_1_rd1out), .RD2out(e_register_1_rd2out), .RtE_2(e_register_1_rte_2),
    .RdE_2(e_register_1_rde_2), .SignImmE(e_register_1_signimme), .PCPlus4E(e_register_1_pcplus4e),
    .reset(reset), .JalD(controller_1_jald), .RegWriteE(e_register_1_regwritee));
  EXT ext_1 (.Imm(jal_instrd[15:0]), .EXTOp(controller_1_extop), .Ext(ext_1_ext));
  Multiplexer #(.select(2), .width(5)) multiplexer_5 (
    .in0(e_register_1_rte_2), .in1(e_register_1_rde_2), .in2({5{1'b1}}), .out(multiplexer_5_out),
    .sel(e_register_1_regdste));  // open: in3, en
  Multiplexer #(.width(32)) multiplexer_6 (
    .in0(e_register_1_rd2out), .in1(e_register_1_signimme), .out(multiplexer_6_out),
    .sel(e_register_1_alusrce));  // open: en
  sll2 sll2_2 (.in_1(e_register_1_signimme), .out_2(sll2_2_out_2));
  ALU alu_1 (
    .ALUOp(e_register_1_alucontrole), .A(e_register_1_rd1out), .B(multiplexer_6_out), .C(alu_1_c),
    .Zero(alu_1_zero));
  Adder #(.width(32)) adder_3 (.a(sll2_2_out_2), .b(e_register_1_pcplus4e), .out(adder_3_out));  // open: cin, cout
  M_register m_register_1 (
    .RegWriteE(e_register_1_regwritee_2), .MemtoRegE(e_register_1_memtorege),
    .MemWriteE(e_register_1_memwritee), .BranchE(e_register_1_branche), .Zero(alu_1_zero), .ALUOut(alu_1_c),
    .WriteDataE(e_register_1_rd2out), .WriteRegE4_0(multiplexer_5_out), .PCBranchE(adder_3_out), .PC_E(pc_e),
    .RegWriteM(m_register_1_regwritem), .MemtoRegM(m_register_1_memtoregm), .MemWriteM(MemWrite),
    .BranchM(m_register_1_branchm), .ZeroM(m_register_1_zerom), .ALUOutM(MemAddr), .WriteDataM(MemData),
    .WriteRegM4_0(m_register_1_writeregm4_0), .PCBranchM(m_register_1_pcbranchm), .PC_M(pc_m_t),
    .reset(reset), .JalE(e_register_1_regwritee), .JalM(m_register_1_jalm));
  and and_1 (and_1_out, m_register_1_branchm, m_register_1_zerom);
  W_register w_register_1 (
    .RegWriteM(m_register_1_regwritem), .MemtoRegM(m_register_1_memtoregm), .ALUOut(MemAddr),
    .WriteDataE(dm_1_rd), .WriteRegE4_0(m_register_1_writeregm4_0), .PC_M(pc_m_t), .RegWriteW(RegWrite),
    .MemtoRegW(w_register_1_memtoregw), .ALUOutW(w_register_1_aluoutw), .ReadDataM(w_register_1_readdatam),
    .WriteRegW4_0(w_register_1_writeregw4_0), .PC_W(pc_w_t), .reset(reset), .JalM(m_register_1_jalm),
    .JalW(JalW));
  DM dm_1 (.A(MemAddr), .RD(dm_1_rd), .reset(reset), .DMWr(MemWrite), .WD(MemData));
  Multiplexer #(.width(32)) multiplexer_7 (
    .in0(w_register_1_aluoutw), .in1(w_register_1_readdatam), .out(multiplexer_7_out),
    .sel(w_register_1_memtoregw));  // open: en

  // Notes on the sheet:
  //   beq
  //   jump
  //   取指令
  //   25:0
  //   25:21
  //   20:16
  //   20:16
  //   15:11
  //   15:0
  //   JumpAddr
  //   译码
  //   执行
  //   存储器
  //   回写
  //   resultW
endmodule

module GRF (
  input  reset,
  input  WE,
  input  [4:0] A1,
  input  [4:0] A2,
  input  [4:0] A3,
  input  [31:0] WD,
  output [31:0] RD1,
  output [31:0] RD2
);

  wire clk, demultiplexer_1_out1, demultiplexer_1_out2, demultiplexer_1_out3, demultiplexer_1_out4,
       demultiplexer_1_out5, demultiplexer_1_out6, demultiplexer_1_out7, demultiplexer_1_out8,
       demultiplexer_1_out9, demultiplexer_1_out10, demultiplexer_1_out11, demultiplexer_1_out12,
       demultiplexer_1_out13, demultiplexer_1_out14, demultiplexer_1_out15, demultiplexer_1_out16,
       demultiplexer_1_out17, demultiplexer_1_out18, demultiplexer_1_out19, demultiplexer_1_out20,
       demultiplexer_1_out21, demultiplexer_1_out22, demultiplexer_1_out23, demultiplexer_1_out24,
       demultiplexer_1_out25, demultiplexer_1_out26, demultiplexer_1_out27, demultiplexer_1_out28,
       demultiplexer_1_out29, demultiplexer_1_out30, demultiplexer_1_out31;
  wire [31:0] a_magical_register_1_out_4, GR1_q, GR2_q, GR3_q, GR4_q, GR5_q, GR6_q, GR7_q, GR8_q, GR9_q,
       GR10_q, GR11_q, GR12_q, GR13_q, GR14_q, GR15_q, GR16_q, GR17_q, GR18_q, GR19_q, GR20_q, GR21_q,
       GR22_q, GR23_q, GR24_q, GR25_q, GR26_q, GR27_q, GR28_q, GR29_q, GR30_q, GR31_q;

  Demultiplexer #(.select(5)) demultiplexer_1 (
    .out1(demultiplexer_1_out1), .out2(demultiplexer_1_out2), .out3(demultiplexer_1_out3),
    .out4(demultiplexer_1_out4), .out5(demultiplexer_1_out5), .out6(demultiplexer_1_out6),
    .out7(demultiplexer_1_out7), .out8(demultiplexer_1_out8), .out9(demultiplexer_1_out9),
    .out10(demultiplexer_1_out10), .out11(demultiplexer_1_out11), .out12(demultiplexer_1_out12),
    .out13(demultiplexer_1_out13), .out14(demultiplexer_1_out14), .out15(demultiplexer_1_out15),
    .out16(demultiplexer_1_out16), .out17(demultiplexer_1_out17), .out18(demultiplexer_1_out18),
    .out19(demultiplexer_1_out19), .out20(demultiplexer_1_out20), .out21(demultiplexer_1_out21),
    .out22(demultiplexer_1_out22), .out23(demultiplexer_1_out23), .out24(demultiplexer_1_out24),
    .out25(demultiplexer_1_out25), .out26(demultiplexer_1_out26), .out27(demultiplexer_1_out27),
    .out28(demultiplexer_1_out28), .out29(demultiplexer_1_out29), .out30(demultiplexer_1_out30),
    .out31(demultiplexer_1_out31), .in(WE), .sel(A3), .en(1'b1));  // open: out0
  Clock clock_1 (.out(clk));
  Register #(.width(32)) GR1 (.D({32{1'b0}}), .Q(GR1_q), .clk(clk), .clr(reset));  // open: en
  Register #(.width(32)) GR2 (.D(WD), .en(demultiplexer_1_out1), .Q(GR2_q), .clk(clk), .clr(reset));
  Register #(.width(32)) GR3 (.D(WD), .en(demultiplexer_1_out2), .Q(GR3_q), .clk(clk), .clr(reset));
  Register #(.width(32)) GR4 (.D(WD), .en(demultiplexer_1_out3), .Q(GR4_q), .clk(clk), .clr(reset));
  Register #(.width(32)) GR5 (.D(WD), .en(demultiplexer_1_out4), .Q(GR5_q), .clk(clk), .clr(reset));
  Register #(.width(32)) GR6 (.D(WD), .en(demultiplexer_1_out5), .Q(GR6_q), .clk(clk), .clr(reset));
  Register #(.width(32)) GR7 (.D(WD), .en(demultiplexer_1_out6), .Q(GR7_q), .clk(clk), .clr(reset));
  Register #(.width(32)) GR8 (.D(WD), .en(demultiplexer_1_out7), .Q(GR8_q), .clk(clk), .clr(reset));
  Register #(.width(32)) GR9 (.D(WD), .en(demultiplexer_1_out8), .Q(GR9_q), .clk(clk), .clr(reset));
  Register #(.width(32)) GR10 (.D(WD), .en(demultiplexer_1_out9), .Q(GR10_q), .clk(clk), .clr(reset));
  Register #(.width(32)) GR11 (.D(WD), .en(demultiplexer_1_out10), .Q(GR11_q), .clk(clk), .clr(reset));
  Register #(.width(32)) GR12 (.D(WD), .en(demultiplexer_1_out11), .Q(GR12_q), .clk(clk), .clr(reset));
  Register #(.width(32)) GR13 (.D(WD), .en(demultiplexer_1_out12), .Q(GR13_q), .clk(clk), .clr(reset));
  Register #(.width(32)) GR14 (.D(WD), .en(demultiplexer_1_out13), .Q(GR14_q), .clk(clk), .clr(reset));
  Register #(.width(32)) GR15 (.D(WD), .en(demultiplexer_1_out14), .Q(GR15_q), .clk(clk), .clr(reset));
  Register #(.width(32)) GR16 (.D(WD), .en(demultiplexer_1_out15), .Q(GR16_q), .clk(clk), .clr(reset));
  Register #(.width(32)) GR17 (.D(WD), .en(demultiplexer_1_out16), .Q(GR17_q), .clk(clk), .clr(reset));
  Register #(.width(32)) GR18 (.D(WD), .en(demultiplexer_1_out17), .Q(GR18_q), .clk(clk), .clr(reset));
  Register #(.width(32)) GR19 (.D(WD), .en(demultiplexer_1_out18), .Q(GR19_q), .clk(clk), .clr(reset));
  Register #(.width(32)) GR20 (.D(WD), .en(demultiplexer_1_out19), .Q(GR20_q), .clk(clk), .clr(reset));
  Register #(.width(32)) GR21 (.D(WD), .en(demultiplexer_1_out20), .Q(GR21_q), .clk(clk), .clr(reset));
  Register #(.width(32)) GR22 (.D(WD), .en(demultiplexer_1_out21), .Q(GR22_q), .clk(clk), .clr(reset));
  Register #(.width(32)) GR23 (.D(WD), .en(demultiplexer_1_out22), .Q(GR23_q), .clk(clk), .clr(reset));
  Register #(.width(32)) GR24 (.D(WD), .en(demultiplexer_1_out23), .Q(GR24_q), .clk(clk), .clr(reset));
  Register #(.width(32)) GR25 (.D(WD), .en(demultiplexer_1_out24), .Q(GR25_q), .clk(clk), .clr(reset));
  Register #(.width(32)) GR26 (.D(WD), .en(demultiplexer_1_out25), .Q(GR26_q), .clk(clk), .clr(reset));
  Register #(.width(32)) GR27 (.D(WD), .en(demultiplexer_1_out26), .Q(GR27_q), .clk(clk), .clr(reset));
  Register #(.width(32)) GR28 (.D(WD), .en(demultiplexer_1_out27), .Q(GR28_q), .clk(clk), .clr(reset));
  Register #(.width(32)) GR29 (.D(WD), .en(demultiplexer_1_out28), .Q(GR29_q), .clk(clk), .clr(reset));
  Register #(.width(32)) GR30 (.D(WD), .en(demultiplexer_1_out29), .Q(GR30_q), .clk(clk), .clr(reset));
  Register #(.width(32)) GR31 (.D(WD), .en(demultiplexer_1_out30), .Q(GR31_q), .clk(clk), .clr(reset));
  A_magical_register a_magical_register_1 (
    .in_2(WD), .reset(reset), .out_4(a_magical_register_1_out_4), .WE(demultiplexer_1_out31));
  Register #(.width(32)) GR32 ();  // open: D, en, Q, clk, clr
  Multiplexer #(.select(5), .width(32)) multiplexer_1 (
    .in0(GR1_q), .in1(GR2_q), .in2(GR3_q), .in3(GR4_q), .in4(GR5_q), .in5(GR6_q), .in6(GR7_q), .in7(GR8_q),
    .in8(GR9_q), .in9(GR10_q), .in10(GR11_q), .in11(GR12_q), .in12(GR13_q), .in13(GR14_q), .in14(GR15_q),
    .in15(GR16_q), .in16(GR17_q), .in17(GR18_q), .in18(GR19_q), .in19(GR20_q), .in20(GR21_q), .in21(GR22_q),
    .in22(GR23_q), .in23(GR24_q), .in24(GR25_q), .in25(GR26_q), .in26(GR27_q), .in27(GR28_q), .in28(GR29_q),
    .in29(GR30_q), .in30(GR31_q), .in31(a_magical_register_1_out_4), .out(RD1), .sel(A1), .en(1'b1));
  // Probe on A1
  // Probe on A2
  Multiplexer #(.select(5), .width(32)) multiplexer_2 (
    .in0(GR1_q), .in1(GR2_q), .in2(GR3_q), .in3(GR4_q), .in4(GR5_q), .in5(GR6_q), .in6(GR7_q), .in7(GR8_q),
    .in8(GR9_q), .in9(GR10_q), .in10(GR11_q), .in11(GR12_q), .in12(GR13_q), .in13(GR14_q), .in14(GR15_q),
    .in15(GR16_q), .in16(GR17_q), .in17(GR18_q), .in18(GR19_q), .in19(GR20_q), .in20(GR21_q), .in21(GR22_q),
    .in22(GR23_q), .in23(GR24_q), .in24(GR25_q), .in25(GR26_q), .in26(GR27_q), .in27(GR28_q), .in28(GR29_q),
    .in29(GR30_q), .in30(GR31_q), .in31(a_magical_register_1_out_4), .out(RD2), .sel(A2), .en(1'b1));
endmodule

module PC (
  input  [31:0] Di,
  input  Reset,
  output [31:0] Do
);

  wire a_magical_register_1_p2;

  // A_magical_register a_magical_register_1: pin names not known; wires that end beside it: Di, a_magical_register_1_p2, Reset, Do
  Clock clock_1 (.out(a_magical_register_1_p2));
endmodule

module EXT (
  input  [15:0] Imm,
  input  [1:0] EXTOp,
  output [31:0] Ext
);

  wire [31:0] bit_extender_1_out, bit_extender_2_out;

  assign bit_extender_1_out = {{16{1'b0}}, Imm};  // Bit_Extender bit_extender_1
  assign bit_extender_2_out = {{16{Imm[15]}}, Imm};  // Bit_Extender bit_extender_2
  Multiplexer #(.select(2), .width(32)) multiplexer_1 (
    .in0(bit_extender_1_out), .in1(bit_extender_2_out), .in2({Imm, {16{1'b0}}}), .out(Ext), .sel(EXTOp));  // open: in3, en
endmodule

module IM (
  input  [31:0] A,
  output [31:0] D
);

  wire [31:0] subtractor_1_out;

  Subtractor #(.width(32)) subtractor_1 (.a(A), .b(32'h3000), .out(subtractor_1_out));  // open: bin, bout
  ROM #(.addrWidth(10), .dataWidth(32)) rom_1 (.addr(subtractor_1_out[11:2]), .data(D), .sel(1'b1));

  // Notes on the sheet:
  //   contents of rom_1 (hex, n*v repeats v):
  //   340f98f8 4*0 3c0eabd3 4*0 3c0d0bc6 4*0 1cf6021 4*0 18d5823 4*0 3410ff98 4*0 3c10ffff 4*0 120b000e
  //   4*0 34070001 4*0 8000c3c 4*0 34080001 4*0 34090001 4*0 340a0001 4*0 c000c50 4*0 340b0001 4*0 8000c69
  //   4*0 340c0001 4*0 10000009 4*0 35ed0001 4*0 3c0f2390 4*0 3e00008
endmodule

module DM (
  input  [31:0] A,
  input  reset,
  input  [31:0] WD,
  input  DMWr,
  output [31:0] RD
);

  wire clock_1_out;

  Clock clock_1 (.out(clock_1_out));
  RAM #(.addrWidth(10), .dataWidth(32), .bus("separate")) ram_1 (
    .addr(A[11:2]), .din(WD), .data(RD), .str(DMWr), .clk(clock_1_out), .ld(1'b1), .clr(reset));  // open: sel
endmodule

module ALU (
  input  [1:0] ALUOp,
  input  [31:0] A,
  input  [31:0] B,
  output [31:0] C,
  output Zero
);

  wire alucontroller_1_cin, alucontroller_1_grf_a3sel, alucontroller_1_grf_wdsel;
  wire [31:0] adder_1_out, multiplexer_1_out, not_1_out, or_1_out;

  assign or_1_out = B | A;  // OR_Gate or_1, 32 bits wide
  ALUController alucontroller_1 (
    .ALUOp(ALUOp), .GRF_A3Sel(alucontroller_1_grf_a3sel), .Cin(alucontroller_1_cin),
    .GRF_WDSel(alucontroller_1_grf_wdsel));  // open: SExt
  assign not_1_out = ~B;  // NOT_Gate not_1, 32 bits wide
  Multiplexer #(.width(32)) multiplexer_1 (
    .in0(B), .in1(not_1_out), .out(multiplexer_1_out), .sel(alucontroller_1_grf_a3sel));  // open: en
  Adder #(.width(32)) adder_1 (
    .a(A), .b(multiplexer_1_out), .out(adder_1_out), .cin(alucontroller_1_cin));  // open: cout
  Comparator #(.width(32)) comparator_1 (.a(adder_1_out), .b({32{1'b0}}), .eq(Zero));  // open: gt, lt
  Multiplexer #(.width(32)) multiplexer_2 (
    .in0(adder_1_out), .in1(or_1_out), .out(C), .sel(alucontroller_1_grf_wdsel));  // open: en
endmodule

module ALUController (
  input  [1:0] ALUOp,
  output SExt,
  output GRF_A3Sel,
  output Cin,
  output GRF_WDSel
);

  wire not_2_out, not_3_out;

  not not_1 (SExt, ALUOp[1]);
  not not_2 (not_2_out, ALUOp[1]);
  not not_3 (not_3_out, ALUOp[1]);
  and and_1 (GRF_WDSel, ALUOp[0], ALUOp[1]);
  and and_2 (GRF_A3Sel, ALUOp[0], not_2_out);
  and and_3 (Cin, ALUOp[0], not_3_out);
endmodule

module or_logic (
  input  addu,
  input  subu,
  input  ori,
  input  lw,
  input  sw,
  input  beq,
  input  lui,
  input  jal,
  input  j,
  input  jr,
  output BranchD,
  output JalD,
  output RegWriteD,
  output EXTOp1,
  output EXTOp2,
  output ALUControl1,
  output ALUControl2,
  output MemWriteD,
  output RegDstD1,
  output RegDstD2,
  output JumpD1,
  output JumpD2,
  output MemtoRegD,
  output ALUSrcD
);

  buf or_1 (BranchD, beq);  // OR_Gate
  buf or_2 (JalD, jal);  // OR_Gate
  or or_3 (RegWriteD, addu, subu, ori, lw, lui, jal);
  buf or_4 (EXTOp1, lui);  // OR_Gate
  or or_5 (EXTOp2, lw, sw, beq);
  buf or_6 (ALUControl1, ori);  // OR_Gate
  or or_7 (ALUControl2, subu, ori, beq);
  buf or_8 (MemWriteD, sw);  // OR_Gate
  buf or_9 (RegDstD1, jal);  // OR_Gate
  or or_10 (RegDstD2, addu, subu);
  buf or_11 (JumpD1, jr);  // OR_Gate
  or or_12 (JumpD2, j, jal);
  buf or_13 (MemtoRegD, lw);  // OR_Gate
  or or_14 (ALUSrcD, sw, ori, lw, lui);
endmodule

module Controller (
  input  [5:0] opcode,
  input  [5:0] funct,
  output [1:0] EXTOp,
  output MemWriteD,
  output MemtoRegD,
  output JalD,
  output [1:0] RegDstD,
  output [1:0] ALUControl,
  output [1:0] JumpD,
  output BranchD,
  output RegWriteD,
  output ALUSrcD
);

  wire addu, addu_out, Beq, j, jal, jr, jr_out, lui, lw, not_1_out, not_2_out, not_3_out, not_4_out,
       not_5_out, not_6_out, not_7_out, not_8_out, not_9_out, not_10_out, not_11_out, not_12_out, not_13_out,
       not_14_out, not_15_out, not_16_out, not_17_out, not_18_out, not_19_out, not_20_out, not_21_out,
       not_22_out, not_23_out, not_24_out, not_25_out, not_26_out, not_27_out, not_28_out, not_29_out,
       not_30_out, not_31_out, not_32_out, not_33_out, not_34_out, not_35_out, not_36_out, not_37_out,
       not_38_out, not_39_out, not_40_out, not_41_out, not_42_out, Ori, R, subu, subu_out, sw;

  not not_1 (not_1_out, opcode[0]);
  not not_2 (not_2_out, opcode[1]);
  not not_3 (not_3_out, opcode[5]);
  not not_4 (not_4_out, opcode[2]);
  not not_5 (not_5_out, opcode[4]);
  not not_6 (not_6_out, opcode[3]);
  and u_R (R, not_1_out, not_2_out, not_4_out, not_6_out, not_5_out, not_3_out);
  not not_7 (not_7_out, funct[1]);
  not not_8 (not_8_out, funct[3]);
  not not_9 (not_9_out, funct[4]);
  not not_10 (not_10_out, funct[2]);
  and u_addu (addu_out, funct[0], not_7_out, not_10_out, not_8_out, not_9_out, funct[5]);
  and and_1 (addu, addu_out, R);
  not not_11 (not_11_out, opcode[0]);
  not not_12 (not_12_out, opcode[1]);
  and u_Beq (Beq, not_11_out, not_12_out, opcode[2], not_14_out, not_15_out, not_13_out);
  not not_13 (not_13_out, opcode[5]);
  not not_14 (not_14_out, opcode[3]);
  not not_15 (not_15_out, opcode[4]);
  not not_16 (not_16_out, funct[3]);
  not not_17 (not_17_out, funct[4]);
  not not_18 (not_18_out, funct[2]);
  and u_subu (subu_out, funct[0], funct[1], not_18_out, not_16_out, not_17_out, funct[5]);
  and and_2 (subu, subu_out, R);
  not not_19 (not_19_out, opcode[5]);
  not not_20 (not_20_out, opcode[1]);
  not not_21 (not_21_out, opcode[4]);
  and u_Ori (Ori, opcode[0], not_20_out, opcode[2], opcode[3], not_21_out, not_19_out);
  not not_22 (not_22_out, funct[4]);
  not not_23 (not_23_out, funct[2]);
  not not_24 (not_24_out, funct[0]);
  not not_25 (not_25_out, funct[1]);
  and u_jr (jr_out, not_24_out, not_25_out, not_23_out, funct[3], not_22_out, not_27_out);
  and and_3 (jr, jr_out, R);
  not not_26 (not_26_out, opcode[2]);
  and u_lw (lw, opcode[0], opcode[1], not_26_out, not_29_out, not_28_out, opcode[5]);
  not not_27 (not_27_out, funct[5]);
  or_logic or_logic_1 (
    .addu(addu), .subu(subu), .ori(Ori), .lw(lw), .sw(sw), .beq(Beq), .lui(lui), .jal(jal), .j(j), .jr(jr),
    .BranchD(BranchD), .JalD(JalD), .RegWriteD(RegWriteD), .EXTOp1(EXTOp[1]), .EXTOp2(EXTOp[0]),
    .ALUControl1(ALUControl[1]), .ALUControl2(ALUControl[0]), .MemWriteD(MemWriteD), .RegDstD1(RegDstD[1]),
    .RegDstD2(RegDstD[0]), .JumpD1(JumpD[1]), .JumpD2(JumpD[0]), .MemtoRegD(MemtoRegD), .ALUSrcD(ALUSrcD));
  not not_28 (not_28_out, opcode[4]);
  not not_29 (not_29_out, opcode[3]);
  not not_30 (not_30_out, opcode[4]);
  not not_31 (not_31_out, opcode[2]);
  and u_sw (sw, opcode[0], opcode[1], not_31_out, opcode[3], not_30_out, opcode[5]);
  and u_lui (lui, opcode[0], opcode[1], opcode[2], opcode[3], not_33_out, not_32_out);
  not not_32 (not_32_out, opcode[5]);
  not not_33 (not_33_out, opcode[4]);
  not not_34 (not_34_out, opcode[3]);
  not not_35 (not_35_out, opcode[4]);
  not not_36 (not_36_out, opcode[0]);
  not not_37 (not_37_out, opcode[2]);
  not not_38 (not_38_out, opcode[5]);
  and u_j (j, not_36_out, opcode[1], not_37_out, not_34_out, not_35_out, not_38_out);
  not not_39 (not_39_out, opcode[2]);
  and u_jal (jal, opcode[0], opcode[1], not_39_out, not_40_out, not_41_out, not_42_out);
  not not_40 (not_40_out, opcode[3]);
  not not_41 (not_41_out, opcode[4]);
  not not_42 (not_42_out, opcode[5]);
endmodule

module D_register (
  input  [31:0] PC_W,
  input  [31:0] IM_D,
  input  [31:0] PCPlus4F,
  input  reset,
  output [31:0] PC_D,
  output [31:0] InstrD,
  output [31:0] PCPlus4D
);

  wire clock_1_out;

  A_magical_register a_magical_register_1 (.in_2(PC_W), .reset(reset), .out_4(PC_D));  // open: WE
  Register #(.width(32)) register_1 (.D(IM_D), .Q(InstrD), .clk(clock_1_out), .clr(reset));  // open: en
  Register #(.width(32)) register_2 (.D(PCPlus4F), .Q(PCPlus4D), .clk(clock_1_out), .clr(reset));  // open: en
  Clock clock_1 (.out(clock_1_out));
endmodule

module E_register (
  input  JalD,
  input  RegWriteD,
  input  MemtoRegD,
  input  MemWriteD,
  input  BranchD,
  input  [1:0] ALUControlD,
  input  ALUSrcD,
  input  [1:0] RegDstD,
  input  [31:0] PC_D,
  input  [31:0] RD1,
  input  [31:0] RD2,
  input  [4:0] rtE,
  input  [4:0] rdE,
  input  [31:0] Signext,
  input  [31:0] PCPlus4D,
  input  reset,
  output RegWriteE,
  output RegWriteE_2,
  output MemtoRegE,
  output MemWriteE,
  output BranchE,
  output [1:0] ALUControlE,
  output ALUSrcE,
  output [1:0] RegDstE,
  output [31:0] PC_E,
  output [31:0] RD1out,
  output [31:0] RD2out,
  output [4:0] RtE_2,
  output [4:0] RdE_2,
  output [31:0] SignImmE,
  output [31:0] PCPlus4E
);

  wire clock_1_out;

  Clock clock_1 (.out(clock_1_out));
  Register #(.width(1)) register_1 (.D(JalD), .Q(RegWriteE), .clk(clock_1_out), .clr(reset));  // open: en
  Register #(.width(1)) register_2 (.D(RegWriteD), .Q(RegWriteE_2), .clk(clock_1_out), .clr(reset));  // open: en
  Register #(.width(1)) register_3 (.D(MemtoRegD), .Q(MemtoRegE), .clk(clock_1_out), .clr(reset));  // open: en
  Register #(.width(1)) register_4 (.D(MemWriteD), .Q(MemWriteE), .clk(clock_1_out), .clr(reset));  // open: en
  Register #(.width(1)) register_5 (.D(BranchD), .Q(BranchE), .clk(clock_1_out), .clr(reset));  // open: en
  Register #(.width(2)) register_6 (.D(ALUControlD), .Q(ALUControlE), .clk(clock_1_out), .clr(reset));  // open: en
  Register #(.width(1)) register_7 (.D(ALUSrcD), .Q(ALUSrcE), .clk(clock_1_out), .clr(reset));  // open: en
  Register #(.width(2)) register_8 (.D(RegDstD), .Q(RegDstE), .clk(clock_1_out), .clr(reset));  // open: en
  A_magical_register a_magical_register_1 (.in_2(PC_D), .reset(reset), .out_4(PC_E));  // open: WE
  Register #(.width(32)) register_9 (.D(RD1), .Q(RD1out), .clk(clock_1_out), .clr(reset));  // open: en
  Register #(.width(32)) register_10 (.D(RD2), .Q(RD2out), .clk(clock_1_out), .clr(reset));  // open: en
  Register #(.width(5)) register_11 (.D(rtE), .Q(RtE_2), .clk(clock_1_out), .clr(reset));  // open: en
  Register #(.width(5)) register_12 (.D(rdE), .Q(RdE_2), .clk(clock_1_out), .clr(reset));  // open: en
  Register #(.width(32)) register_13 (.D(Signext), .Q(SignImmE), .clk(clock_1_out), .clr(reset));  // open: en
  Register #(.width(32)) register_14 (.D(PCPlus4D), .Q(PCPlus4E), .clk(clock_1_out), .clr(reset));  // open: en
endmodule

module M_register (
  input  reset,
  input  JalE,
  input  RegWriteE,
  input  MemtoRegE,
  input  MemWriteE,
  input  BranchE,
  input  Zero,
  input  [31:0] ALUOut,
  input  [31:0] WriteDataE,
  input  [4:0] WriteRegE4_0,
  input  [31:0] PCBranchE,
  input  [31:0] PC_E,
  output JalM,
  output RegWriteM,
  output MemtoRegM,
  output MemWriteM,
  output BranchM,
  output ZeroM,
  output [31:0] ALUOutM,
  output [31:0] WriteDataM,
  output [4:0] WriteRegM4_0,
  output [31:0] PCBranchM,
  output [31:0] PC_M
);

  wire clock_1_out;

  Clock clock_1 (.out(clock_1_out));
  Register #(.width(1)) register_1 (.D(JalE), .Q(JalM), .clk(clock_1_out), .clr(reset));  // open: en
  Register #(.width(1)) register_2 (.D(RegWriteE), .Q(RegWriteM), .clk(clock_1_out), .clr(reset));  // open: en
  Register #(.width(1)) register_3 (.D(MemtoRegE), .Q(MemtoRegM), .clk(clock_1_out), .clr(reset));  // open: en
  Register #(.width(1)) register_4 (.D(MemWriteE), .Q(MemWriteM), .clk(clock_1_out), .clr(reset));  // open: en
  Register #(.width(1)) register_5 (.D(BranchE), .Q(BranchM), .clk(clock_1_out), .clr(reset));  // open: en
  Register #(.width(1)) register_6 (.D(Zero), .Q(ZeroM), .clk(clock_1_out), .clr(reset));  // open: en
  Register #(.width(32)) register_7 (.D(ALUOut), .Q(ALUOutM), .clk(clock_1_out), .clr(reset));  // open: en
  Register #(.width(32)) register_8 (.D(WriteDataE), .Q(WriteDataM), .clk(clock_1_out), .clr(reset));  // open: en
  Register #(.width(5)) register_9 (.D(WriteRegE4_0), .Q(WriteRegM4_0), .clk(clock_1_out), .clr(reset));  // open: en
  Register #(.width(32)) register_10 (.D(PCBranchE), .Q(PCBranchM), .clk(clock_1_out), .clr(reset));  // open: en
  A_magical_register a_magical_register_1 (.in_2(PC_E), .reset(reset), .out_4(PC_M));  // open: WE
endmodule

module W_register (
  input  reset,
  input  JalM,
  input  RegWriteM,
  input  MemtoRegM,
  input  [31:0] ALUOut,
  input  [31:0] WriteDataE,
  input  [4:0] WriteRegE4_0,
  input  [31:0] PC_M,
  output JalW,
  output RegWriteW,
  output MemtoRegW,
  output [31:0] ALUOutW,
  output [31:0] ReadDataM,
  output [4:0] WriteRegW4_0,
  output [31:0] PC_W
);

  wire clock_1_out;

  Clock clock_1 (.out(clock_1_out));
  Register #(.width(1)) register_1 (.D(JalM), .Q(JalW), .clk(clock_1_out), .clr(reset));  // open: en
  Register #(.width(1)) register_2 (.D(RegWriteM), .Q(RegWriteW), .clk(clock_1_out), .clr(reset));  // open: en
  Register #(.width(1)) register_3 (.D(MemtoRegM), .Q(MemtoRegW), .clk(clock_1_out), .clr(reset));  // open: en
  Register #(.width(32)) register_4 (.D(ALUOut), .Q(ALUOutW), .clk(clock_1_out), .clr(reset));  // open: en
  Register #(.width(32)) register_5 (.D(WriteDataE), .Q(ReadDataM), .clk(clock_1_out), .clr(reset));  // open: en
  Register #(.width(5)) register_6 (.D(WriteRegE4_0), .Q(WriteRegW4_0), .clk(clock_1_out), .clr(reset));  // open: en
  A_magical_register a_magical_register_1 (.in_2(PC_M), .reset(reset), .out_4(PC_W));  // open: WE
endmodule

module sll2 (
  input  [31:0] in_1,
  output [31:0] out_2
);


  assign out_2 = {4'b0000, in_1[25:0], 2'b00};
endmodule

module test (
);

  wire main_1_memwrite, main_1_regwrite;
  wire [4:0] main_1_regaddr;
  wire [31:0] main_1_memaddr, main_1_memdata, main_1_pc_m, main_1_pc_w, main_1_regdata;

  main main_1 (
    .pc_m(main_1_pc_m), .RegWrite(main_1_regwrite), .RegAddr(main_1_regaddr), .RegData(main_1_regdata),
    .pc_w(main_1_pc_w), .MemWrite(main_1_memwrite), .MemAddr(main_1_memaddr), .MemData(main_1_memdata));  // open: reset
  // Probe on main_1_memdata
  // Probe on main_1_pc_w
  // Probe on main_1_pc_m
  // Probe on main_1_regwrite
  // Probe on main_1_regaddr
  // Probe on main_1_memaddr
  // Probe on main_1_regdata
  // Probe on main_1_memwrite
endmodule

module A_magical_register (
  input  WE,
  input  [31:0] in_2,
  input  reset,
  output [31:0] out_4
);

  wire clock_1_out, counter_1_q, register_1_q;
  wire [31:0] multiplexer_1_out, pull_resistor_1_node, register_2_q;

  Multiplexer #(.width(32)) multiplexer_1 (
    .in0(out_4), .in1(in_2), .out(multiplexer_1_out), .sel(register_1_q));  // open: en
  Register #(.width(1), .trigger("falling")) register_1 (
    .D(counter_1_q), .Q(register_1_q), .clk(clock_1_out));  // open: en, clr
  Pull_Resistor pull_resistor_1 (.node(pull_resistor_1_node));
  Register #(.width(32)) register_2 (.D(multiplexer_1_out), .en(WE), .Q(register_2_q), .clk(clock_1_out), .clr(reset));
  Counter #(.width(1), .max('h1), .ongoal("stay")) counter_1 (
    .Q(counter_1_q), .clk(clock_1_out));  // open: load, D, count, carry, clr
  Clock clock_1 (.out(clock_1_out));
  Multiplexer #(.width(32)) multiplexer_2 (
    .in0(pull_resistor_1_node), .in1(register_2_q), .out(out_4), .sel(counter_1_q));  // open: en
  // also tied to GND on the sheet: {pull_resistor_1_node[0], pull_resistor_1_node[1], pull_resistor_1_node[2], pull_resistor_1_node[3], pull_resistor_1_node[4], pull_resistor_1_node[5], pull_resistor_1_node[6], pull_resistor_1_node[7], pull_resistor_1_node[8], pull_resistor_1_node[9], pull_resistor_1_node[10], pull_resistor_1_node[11], pull_resistor_1_node[14], pull_resistor_1_node[15], pull_resistor_1_node[16], pull_resistor_1_node[17], pull_resistor_1_node[18], pull_resistor_1_node[19], pull_resistor_1_node[20], pull_resistor_1_node[21], pull_resistor_1_node[22], pull_resistor_1_node[23], pull_resistor_1_node[24], pull_resistor_1_node[25], pull_resistor_1_node[26], pull_resistor_1_node[27], pull_resistor_1_node[28], pull_resistor_1_node[29], pull_resistor_1_node[30], pull_resistor_1_node[31]}
  // also tied to VCC on the sheet: {pull_resistor_1_node[12], pull_resistor_1_node[13]}
endmodule
