// Logisim project Logisim_4BitSort.circ as structural Verilog: 3 circuits, main circuit 1bit_swap
module _1bit_swap (
  input  I1,
  input  I2,
  input  S,
  output O1,
  output O2
);

  wire and_1_out, and_2_out, and_3_out, and_4_out, not_1_out, not_2_out;

  not not_1 (not_1_out, S);
  not not_2 (not_2_out, S);
  and and_1 (and_1_out, I2, S);
  and and_2 (and_2_out, I1, not_1_out);
  and and_3 (and_3_out, I2, not_2_out);
  and and_4 (and_4_out, I1, S);
  or or_1 (O1, and_1_out, and_2_out);
  or or_2 (O2, and_3_out, and_4_out);
endmodule

module _4bit_swap (
  input  [3:0] I41,
  input  [3:0] I42,
  output [3:0] O41,
  output [3:0] O42
);

  wire comparator_1_gt;

  Comparator #(.width(4), .mode("unsigned")) comparator_1 (.a(I41), .b(I42), .gt(comparator_1_gt));  // open: eq, lt
  _1bit_swap u_1bit_swap_1 (.I1(I41[0]), .I2(I42[0]), .S(comparator_1_gt), .O1(O41[0]), .O2(O42[0]));
  _1bit_swap u_1bit_swap_2 (.I1(I41[1]), .I2(I42[1]), .S(comparator_1_gt), .O1(O41[1]), .O2(O42[1]));
  _1bit_swap u_1bit_swap_3 (.I1(I41[2]), .I2(I42[2]), .S(comparator_1_gt), .O1(O41[2]), .O2(O42[2]));
  _1bit_swap u_1bit_swap_4 (.I1(I41[3]), .I2(I42[3]), .S(comparator_1_gt), .O1(O41[3]), .O2(O42[3]));
endmodule

module _4bit_sort (
  input  [3:0] A,
  input  [3:0] B,
  input  [3:0] C,
  input  [3:0] D,
  output [3:0] _1,
  output [3:0] _2,
  output [3:0] _3,
  output [3:0] _4
);

  wire [3:0] n4bit_swap_1_o41, n4bit_swap_1_o42, n4bit_swap_2_o41, n4bit_swap_2_o42, n4bit_swap_3_o42,
       n4bit_swap_4_o41;

  _4bit_swap u_4bit_swap_1 (.I41(A), .I42(B), .O41(n4bit_swap_1_o41), .O42(n4bit_swap_1_o42));
  _4bit_swap u_4bit_swap_2 (.I41(C), .I42(D), .O41(n4bit_swap_2_o41), .O42(n4bit_swap_2_o42));
  _4bit_swap u_4bit_swap_3 (.I41(n4bit_swap_1_o41), .I42(n4bit_swap_2_o41), .O41(_1), .O42(n4bit_swap_3_o42));
  _4bit_swap u_4bit_swap_4 (.I41(n4bit_swap_1_o42), .I42(n4bit_swap_2_o42), .O41(n4bit_swap_4_o41), .O42(_4));
  _4bit_swap u_4bit_swap_5 (.I41(n4bit_swap_3_o42), .I42(n4bit_swap_4_o41), .O41(_2), .O42(_3));
endmodule
