// Logisim project P0_L0_4BitAlu.circ as structural Verilog: 6 circuits, main circuit alu
module alu (
  input  [3:0] A,
  input  [3:0] B,
  input  [1:0] ALUOp,
  output [3:0] C
);

  wire [3:0] add_out, and1_1_out_3, or_1_out_3, sub_out;

  add add (.In1(A), .In2(B), .Out(add_out));
  sub sub (.In1(A), .In2(B), .Out(sub_out));
  and1 and1_1 (.In1(A), .in_2(B), .out_3(and1_1_out_3));
  \or  or_1 (.In1(A), .In2(B), .out_3(or_1_out_3));
  Multiplexer #(.select(2), .width(4)) multiplexer_1 (
    .in0(add_out), .in1(sub_out), .in2(and1_1_out_3), .in3(or_1_out_3), .out(C), .sel(ALUOp));  // open: en
endmodule

module add (
  input  [3:0] In1,
  input  [3:0] In2,
  output [3:0] Out
);

  wire n1bitadd_1_carryout, n1bitadd_2_carryout, n1bitadd_3_carryout;

  _1bitadd u_1bitadd_1 (.in1(In1[0]), .in2(In2[0]), .carryin(1'b0), .out(Out[0]), .carryout(n1bitadd_1_carryout));
  _1bitadd u_1bitadd_2 (
    .in1(In1[1]), .in2(In2[1]), .carryin(n1bitadd_1_carryout), .out(Out[1]), .carryout(n1bitadd_2_carryout));
  _1bitadd u_1bitadd_3 (
    .in1(In1[2]), .in2(In2[2]), .carryin(n1bitadd_2_carryout), .out(Out[2]), .carryout(n1bitadd_3_carryout));
  _1bitadd u_1bitadd_4 (.in1(In1[3]), .in2(In2[3]), .carryin(n1bitadd_3_carryout), .out(Out[3]));  // open: carryout
endmodule

module _1bitadd (
  input  in1,
  input  in2,
  input  carryin,
  output out,
  output carryout
);

  wire and_1_out, and_2_out, and_3_out, and_4_out, and_5_out, and_6_out, and_7_out, and_8_out, and_9_out,
       and_10_out, and_11_out, not_1_out, not_2_out, not_3_out, not_4_out, not_5_out, not_6_out, or_1_out,
       or_3_out, or_4_out;

  not not_1 (not_1_out, in1);
  not not_2 (not_2_out, in2);
  not not_3 (not_3_out, in1);
  not not_4 (not_4_out, in2);
  and and_1 (and_1_out, in2, carryin);
  and and_2 (and_2_out, in1, carryin);
  and and_3 (and_3_out, not_1_out, not_2_out);
  and and_4 (and_4_out, not_3_out, in2);
  not not_5 (not_5_out, carryin);
  and and_5 (and_5_out, in1, not_4_out);
  not not_6 (not_6_out, carryin);
  and and_6 (and_6_out, in1, in2);
  or or_1 (or_1_out, and_1_out, and_2_out);
  and and_7 (and_7_out, in1, in2);
  and and_8 (and_8_out, and_3_out, carryin);
  and and_9 (and_9_out, and_4_out, not_5_out);
  and and_10 (and_10_out, and_5_out, not_6_out);
  and and_11 (and_11_out, and_6_out, carryin);
  or or_2 (carryout, or_1_out, and_7_out);
  or or_3 (or_3_out, and_8_out, and_9_out);
  or or_4 (or_4_out, and_10_out, and_11_out);
  or or_5 (out, or_3_out, or_4_out);
endmodule

module sub (
  input  [3:0] In1,
  input  [3:0] In2,
  output [3:0] Out
);

  wire [3:0] add_1_out, not_1_out;

  not not_1 (not_1_out[0], In2[0]);
  not not_2 (not_1_out[1], In2[1]);
  not not_3 (not_1_out[2], In2[2]);
  not not_4 (not_1_out[3], In2[3]);
  add add_1 (.In1(4'b0001), .In2(not_1_out), .Out(add_1_out));
  add add_2 (.In1(In1), .In2(add_1_out), .Out(Out));
endmodule

module \or  (
  input  [3:0] In1,
  input  [3:0] In2,
  output [3:0] out_3
);

  or or_1 (out_3[0], In1[0], In2[0]);
  or or_2 (out_3[1], In1[1], In2[1]);
  or or_3 (out_3[2], In1[2], In2[2]);
  or or_4 (out_3[3], In1[3], In2[3]);
endmodule

module and1 (
  input  [3:0] In1,
  input  [3:0] in_2,
  output [3:0] out_3
);

  and and_1 (out_3[0], In1[0], in_2[0]);
  and and_2 (out_3[1], In1[1], in_2[1]);
  and and_3 (out_3[2], In1[2], in_2[2]);
  and and_4 (out_3[3], In1[3], in_2[3]);
endmodule
