// Logisim project P0_L0_CRC.circ as structural Verilog: 3 circuits, main circuit CRC
module CRC (
  input  [7:0] A,
  input  [3:0] B,
  output [10:0] C
);

  _11_4_divider u_11_4_divider_1 (.divided({A, 3'b000}), .divider(B), .left(C[2:0]));  // open: Out

  assign C[10:3] = A;
endmodule

module _4bit_sub (
  input  In1,
  input  Di1,
  input  In2,
  input  Di2,
  input  In3,
  input  Di3,
  input  In4,
  input  Di4,
  output Outbit,
  output Out1,
  output Out2,
  output Out3,
  output Out4
);

  wire xor_1_out, xor_2_out, xor_3_out, xor_4_out;

  xor xor_1 (xor_1_out, In1, Di1);
  xor xor_2 (xor_2_out, In2, Di2);
  xor xor_3 (xor_3_out, In3, Di3);
  xor xor_4 (xor_4_out, In4, Di4);
  Multiplexer multiplexer_1 (.in0(In1), .in1(xor_1_out), .out(Out1), .sel(In1));  // open: en
  Multiplexer multiplexer_2 (.in0(In2), .in1(xor_2_out), .out(Out2), .sel(In1));  // open: en
  Multiplexer multiplexer_3 (.in0(In3), .in1(xor_3_out), .out(Out3), .sel(In1));  // open: en
  Multiplexer multiplexer_4 (.in0(In4), .in1(xor_4_out), .out(Out4), .sel(In1));  // open: en

  assign Outbit = In1;
endmodule

module _11_4_divider (
  input  [10:0] divided,
  input  [3:0] divider,
  output [7:0] Out,
  output [2:0] left
);

  wire n4bit_sub_1_out2, n4bit_sub_1_out3, n4bit_sub_1_out4, n4bit_sub_2_out2, n4bit_sub_2_out3,
       n4bit_sub_2_out4, n4bit_sub_3_out2, n4bit_sub_3_out3, n4bit_sub_3_out4, n4bit_sub_4_out2,
       n4bit_sub_4_out3, n4bit_sub_4_out4, n4bit_sub_5_out2, n4bit_sub_5_out3, n4bit_sub_5_out4,
       n4bit_sub_6_out2, n4bit_sub_6_out3, n4bit_sub_6_out4, n4bit_sub_7_out2, n4bit_sub_7_out3,
       n4bit_sub_7_out4;

  _4bit_sub u_4bit_sub_1 (
    .In1(divided[10]), .In2(divided[9]), .In3(divided[8]), .In4(divided[7]), .Outbit(Out[7]),
    .Di1(divider[3]), .Di2(divider[2]), .Di3(divider[1]), .Di4(divider[0]), .Out2(n4bit_sub_1_out2),
    .Out3(n4bit_sub_1_out3), .Out4(n4bit_sub_1_out4));  // open: Out1
  _4bit_sub u_4bit_sub_2 (
    .In1(n4bit_sub_1_out2), .In2(n4bit_sub_1_out3), .In3(n4bit_sub_1_out4), .In4(divided[6]),
    .Outbit(Out[6]), .Di1(divider[3]), .Di2(divider[2]), .Di3(divider[1]), .Di4(divider[0]),
    .Out2(n4bit_sub_2_out2), .Out3(n4bit_sub_2_out3), .Out4(n4bit_sub_2_out4));  // open: Out1
  _4bit_sub u_4bit_sub_3 (
    .In1(n4bit_sub_2_out2), .In2(n4bit_sub_2_out3), .In3(n4bit_sub_2_out4), .In4(divided[5]),
    .Outbit(Out[5]), .Di1(divider[3]), .Di2(divider[2]), .Di3(divider[1]), .Di4(divider[0]),
    .Out2(n4bit_sub_3_out2), .Out3(n4bit_sub_3_out3), .Out4(n4bit_sub_3_out4));  // open: Out1
  _4bit_sub u_4bit_sub_4 (
    .In1(n4bit_sub_3_out2), .In2(n4bit_sub_3_out3), .In3(n4bit_sub_3_out4), .In4(divided[4]),
    .Outbit(Out[4]), .Di1(divider[3]), .Di2(divider[2]), .Di3(divider[1]), .Di4(divider[0]),
    .Out2(n4bit_sub_4_out2), .Out3(n4bit_sub_4_out3), .Out4(n4bit_sub_4_out4));  // open: Out1
  _4bit_sub u_4bit_sub_5 (
    .In1(n4bit_sub_4_out2), .In2(n4bit_sub_4_out3), .In3(n4bit_sub_4_out4), .In4(divided[3]),
    .Outbit(Out[3]), .Di1(divider[3]), .Di2(divider[2]), .Di3(divider[1]), .Di4(divider[0]),
    .Out2(n4bit_sub_5_out2), .Out3(n4bit_sub_5_out3), .Out4(n4bit_sub_5_out4));  // open: Out1
  _4bit_sub u_4bit_sub_6 (
    .In1(n4bit_sub_5_out2), .In2(n4bit_sub_5_out3), .In3(n4bit_sub_5_out4), .In4(divided[2]),
    .Outbit(Out[2]), .Di1(divider[3]), .Di2(divider[2]), .Di3(divider[1]), .Di4(divider[0]),
    .Out2(n4bit_sub_6_out2), .Out3(n4bit_sub_6_out3), .Out4(n4bit_sub_6_out4));  // open: Out1
  _4bit_sub u_4bit_sub_7 (
    .In1(n4bit_sub_6_out2), .In2(n4bit_sub_6_out3), .In3(n4bit_sub_6_out4), .In4(divided[1]),
    .Outbit(Out[1]), .Di1(divider[3]), .Di2(divider[2]), .Di3(divider[1]), .Di4(divider[0]),
    .Out2(n4bit_sub_7_out2), .Out3(n4bit_sub_7_out3), .Out4(n4bit_sub_7_out4));  // open: Out1
  _4bit_sub u_4bit_sub_8 (
    .In1(n4bit_sub_7_out2), .In2(n4bit_sub_7_out3), .In3(n4bit_sub_7_out4), .In4(divided[0]),
    .Outbit(Out[0]), .Di1(divider[3]), .Di2(divider[2]), .Di3(divider[1]), .Di4(divider[0]), .Out2(left[2]),
    .Out3(left[1]), .Out4(left[0]));  // open: Out1
endmodule
