// Logisim project P0_L0_GRF.circ as structural Verilog: 2 circuits, main circuit grf
module grf (
  input  clk,
  input  reset,
  input  WE,
  input  [4:0] A1,
  input  [4:0] A2,
  input  [4:0] A3,
  input  [31:0] WD,
  output [31:0] RD1,
  output [31:0] RD2
);

  wire demultiplexer_1_out1, demultiplexer_1_out2, demultiplexer_1_out3, demultiplexer_1_out4,
       demultiplexer_1_out5, demultiplexer_1_out6, demultiplexer_1_out7, demultiplexer_1_out8,
       demultiplexer_1_out9, demultiplexer_1_out10, demultiplexer_1_out11, demultiplexer_1_out12,
       demultiplexer_1_out13, demultiplexer_1_out14, demultiplexer_1_out15, demultiplexer_1_out16,
       demultiplexer_1_out17, demultiplexer_1_out18, demultiplexer_1_out19, demultiplexer_1_out20,
       demultiplexer_1_out21, demultiplexer_1_out22, demultiplexer_1_out23, demultiplexer_1_out24,
       demultiplexer_1_out25, demultiplexer_1_out26, demultiplexer_1_out27, demultiplexer_1_out28,
       demultiplexer_1_out29, demultiplexer_1_out30, demultiplexer_1_out31;
  wire [31:0] GR1_q, GR2_q, GR3_q, GR4_q, GR5_q, GR6_q, GR7_q, GR8_q, GR9_q, GR10_q, GR11_q, GR12_q, GR13_q,
       GR14_q, GR15_q, GR16_q, GR17_q, GR18_q, GR19_q, GR20_q, GR21_q, GR22_q, GR23_q, GR24_q, GR25_q,
       GR26_q, GR27_q, GR28_q, GR29_q, GR30_q, GR31_q, GR32_q;

  Demultiplexer #(.select(5)) demultiplexer_1 (
    .out1(demultiplexer_1_out1), .out2(demultiplexer_1_out2), .out3(demultiplexer_1_out3),
    .out4(demultiplexer_1_out4), .out5(demultiplexer_1_out5), .out6(demultiplexer_1_out6),
    .out7(demultiplexer_1_out7), .out8(demultiplexer_1_out8), .out9(demultiplexer_1_out9),
    .out10(demultiplexer_1_out10), .out11(demultiplexer_1_out11), .out12(demultiplexer_1_out12),
    .out13(demultiplexer_1_out13), .out14(demultiplexer_1_out14), .out15(demultiplexer_1_out15),
    .out16(demultiplexer_1_out16), .out17(demultiplexer_1_out17), .out18(demultiplexer_1_out18),
    .out19(demultiplexer_1_out19), .out20(demultiplexer_1_out20), .out21(demultiplexer_1_out21),
    .out22(demultiplexer_1_out22), .out23(demultiplexer_1_out23), .out24(demultiplexer_1_out24),
    .out25(demultiplexer_1_out25), .out26(demultiplexer_1_out26), .out27(demultiplexer_1_out27),
    .out28(demultiplexer_1_out28), .out29(demultiplexer_1_out29), .out30(demultiplexer_1_out30),
    .out31(demultiplexer_1_out31), .in(WE), .sel(A3), .en(1'b1));  // open: out0
  Register #(.width(32)) GR1 (.D({32{1'b0}}), .Q(GR1_q), .clk(clk), .clr(reset));  // open: en
  Register #(.width(32)) GR2 (.D(WD), .en(demultiplexer_1_out1), .Q(GR2_q), .clk(clk), .clr(reset));
  Register #(.width(32)) GR3 (.D(WD), .en(demultiplexer_1_out2), .Q(GR3_q), .clk(clk), .clr(reset));
  Register #(.width(32)) GR4 (.D(WD), .en(demultiplexer_1_out3), .Q(GR4_q), .clk(clk), .clr(reset));
  Register #(.width(32)) GR5 (.D(WD), .en(demultiplexer_1_out4), .Q(GR5_q), .clk(clk), .clr(reset));
  Register #(.width(32)) GR6 (.D(WD), .en(demultiplexer_1_out5), .Q(GR6_q), .clk(clk), .clr(reset));
  Register #(.width(32)) GR7 (.D(WD), .en(demultiplexer_1_out6), .Q(GR7_q), .clk(clk), .clr(reset));
  Register #(.width(32)) GR8 (.D(WD), .en(demultiplexer_1_out7), .Q(GR8_q), .clk(clk), .clr(reset));
  Register #(.width(32)) GR9 (.D(WD), .en(demultiplexer_1_out8), .Q(GR9_q), .clk(clk), .clr(reset));
  Register #(.width(32)) GR10 (.D(WD), .en(demultiplexer_1_out9), .Q(GR10_q), .clk(clk), .clr(reset));
  Register #(.width(32)) GR11 (.D(WD), .en(demultiplexer_1_out10), .Q(GR11_q), .clk(clk), .clr(reset));
  Register #(.width(32)) GR12 (.D(WD), .en(demultiplexer_1_out11), .Q(GR12_q), .clk(clk), .clr(reset));
  Register #(.width(32)) GR13 (.D(WD), .en(demultiplexer_1_out12), .Q(GR13_q), .clk(clk), .clr(reset));
  Register #(.width(32)) GR14 (.D(WD), .en(demultiplexer_1_out13), .Q(GR14_q), .clk(clk), .clr(reset));
  Register #(.width(32)) GR15 (.D(WD), .en(demultiplexer_1_out14), .Q(GR15_q), .clk(clk), .clr(reset));
  Register #(.width(32)) GR16 (.D(WD), .en(demultiplexer_1_out15), .Q(GR16_q), .clk(clk), .clr(reset));
  Register #(.width(32)) GR17 (.D(WD), .en(demultiplexer_1_out16), .Q(GR17_q), .clk(clk), .clr(reset));
  Register #(.width(32)) GR18 (.D(WD), .en(demultiplexer_1_out17), .Q(GR18_q), .clk(clk), .clr(reset));
  Register #(.width(32)) GR19 (.D(WD), .en(demultiplexer_1_out18), .Q(GR19_q), .clk(clk), .clr(reset));
  Register #(.width(32)) GR20 (.D(WD), .en(demultiplexer_1_out19), .Q(GR20_q), .clk(clk), .clr(reset));
  Register #(.width(32)) GR21 (.D(WD), .en(demultiplexer_1_out20), .Q(GR21_q), .clk(clk), .clr(reset));
  Register #(.width(32)) GR22 (.D(WD), .en(demultiplexer_1_out21), .Q(GR22_q), .clk(clk), .clr(reset));
  Register #(.width(32)) GR23 (.D(WD), .en(demultiplexer_1_out22), .Q(GR23_q), .clk(clk), .clr(reset));
  Register #(.width(32)) GR24 (.D(WD), .en(demultiplexer_1_out23), .Q(GR24_q), .clk(clk), .clr(reset));
  Register #(.width(32)) GR25 (.D(WD), .en(demultiplexer_1_out24), .Q(GR25_q), .clk(clk), .clr(reset));
  Register #(.width(32)) GR26 (.D(WD), .en(demultiplexer_1_out25), .Q(GR26_q), .clk(clk), .clr(reset));
  Register #(.width(32)) GR27 (.D(WD), .en(demultiplexer_1_out26), .Q(GR27_q), .clk(clk), .clr(reset));
  Register #(.width(32)) GR28 (.D(WD), .en(demultiplexer_1_out27), .Q(GR28_q), .clk(clk), .clr(reset));
  Register #(.width(32)) GR29 (.D(WD), .en(demultiplexer_1_out28), .Q(GR29_q), .clk(clk), .clr(reset));
  Register #(.width(32)) GR30 (.D(WD), .en(demultiplexer_1_out29), .Q(GR30_q), .clk(clk), .clr(reset));
  Register #(.width(32)) GR31 (.D(WD), .en(demultiplexer_1_out30), .Q(GR31_q), .clk(clk), .clr(reset));
  Register #(.width(32)) GR32 (.D(WD), .en(demultiplexer_1_out31), .Q(GR32_q), .clk(clk), .clr(reset));
  Multiplexer #(.select(5), .width(32)) multiplexer_1 (
    .in0(GR1_q), .in1(GR2_q), .in2(GR3_q), .in3(GR4_q), .in4(GR5_q), .in5(GR6_q), .in6(GR7_q), .in7(GR8_q),
    .in8(GR9_q), .in9(GR10_q), .in10(GR11_q), .in11(GR12_q), .in12(GR13_q), .in13(GR14_q), .in14(GR15_q),
    .in15(GR16_q), .in16(GR17_q), .in17(GR18_q), .in18(GR19_q), .in19(GR20_q), .in20(GR21_q), .in21(GR22_q),
    .in22(GR23_q), .in23(GR24_q), .in24(GR25_q), .in25(GR26_q), .in26(GR27_q), .in27(GR28_q), .in28(GR29_q),
    .in29(GR30_q), .in30(GR31_q), .in31(GR32_q), .out(RD1), .sel(A1), .en(1'b1));
  Multiplexer #(.select(5), .width(32)) multiplexer_2 (
    .in0(GR1_q), .in1(GR2_q), .in2(GR3_q), .in3(GR4_q), .in4(GR5_q), .in5(GR6_q), .in6(GR7_q), .in7(GR8_q),
    .in8(GR9_q), .in9(GR10_q), .in10(GR11_q), .in11(GR12_q), .in12(GR13_q), .in13(GR14_q), .in14(GR15_q),
    .in15(GR16_q), .in16(GR17_q), .in17(GR18_q), .in18(GR19_q), .in19(GR20_q), .in20(GR21_q), .in21(GR22_q),
    .in22(GR23_q), .in23(GR24_q), .in24(GR25_q), .in25(GR26_q), .in26(GR27_q), .in27(GR28_q), .in28(GR29_q),
    .in29(GR30_q), .in30(GR31_q), .in31(GR32_q), .out(RD2), .sel(A2), .en(1'b1));
endmodule

module test (
  output [31:0] out_1,
  output [31:0] out_2,
  output halt
);

  wire clock_1_out;
  wire [7:0] counter_1_q;
  wire [16:0] rom_1_data;
  wire [31:0] rom_2_data;

  Clock clock_1 (.out(clock_1_out));
  Counter counter_1 (.Q(counter_1_q), .carry(halt), .clk(clock_1_out));  // open: load, D, count, clr
  ROM #(.dataWidth(17)) rom_1 (.addr(counter_1_q), .data(rom_1_data));  // open: sel
  ROM #(.dataWidth(32)) rom_2 (.addr(counter_1_q), .data(rom_2_data));  // open: sel
  grf grf (
    .clk(clock_1_out), .reset(rom_1_data[16]), .WE(rom_1_data[15]), .A1(rom_1_data[14:10]),
    .A2(rom_1_data[9:5]), .A3(rom_1_data[4:0]), .WD(rom_2_data), .RD1(out_1), .RD2(out_2));
endmodule
