// Logisim project Logisim_fibonacci(cleaner way).circ as structural Verilog: 3 circuits, main circuit main
module main (
  input  [2:0] in_1,
  output [3:0] out_2
);

  wire output_signal;
  wire [3:0] fib_now;

  counter_logic \u_计数逻辑  (.\input (in_1), .in_2(1'b0), .out_3(output_signal));
  calculate_logic \u_计算逻辑  (.in_1(1'b0), .freeze(output_signal), .out_3(fib_now));
  // Probe on fib_now
  Multiplexer #(.width(4)) multiplexer_1 (.in0(4'b0000), .in1(fib_now), .out(out_2), .sel(output_signal));  // open: en
endmodule

module counter_logic (
  input  [2:0] \input ,
  input  in_2,
  output out_3
);

  wire clk;
  wire [3:0] counter_1_q, max;

  Clock clock_1 (.out(clk));
  Counter #(.width(4), .max('hf)) counter_1 (
    .count(1'b1), .Q(counter_1_q), .clk(clk), .clr(in_2));  // open: load, D, carry
  Comparator #(.width(4)) comparator_1 (.a(max), .b(counter_1_q), .lt(out_3));  // open: gt, eq
  assign max = {{1{1'b0}}, \input };  // Bit_Extender bit_extender_1

  // Other names for the same wires on the sheet: reset = in_2
endmodule

module calculate_logic (
  input  in_1,
  input  freeze,
  output [3:0] out_3
);

  wire clk, enable, initialize;
  wire [3:0] adder_1_out, multiplexer_1_out, prev;

  Clock clock_1 (.out(clk));
  Counter #(.width(1), .max('h1), .ongoal("stay")) counter_1 (
    .Q(initialize), .clk(clk), .clr(in_1));  // open: load, D, count, carry
  not not_1 (enable, freeze);
  Multiplexer #(.width(4)) multiplexer_1 (
    .in0(4'b0001), .in1(out_3), .out(multiplexer_1_out), .sel(initialize));  // open: en
  Adder #(.width(4)) adder_1 (.a(out_3), .b(prev), .out(adder_1_out));  // open: cin, cout
  Register #(.width(4)) u_prev (.D(multiplexer_1_out), .en(enable), .Q(prev), .clk(clk), .clr(in_1));
  Register #(.width(4)) now (.D(adder_1_out), .en(enable), .Q(out_3), .clk(clk), .clr(in_1));

  // Other names for the same wires on the sheet: now[3:0] = out_3; reset = in_1
endmodule
