// Logisim project Logisim_fibonacci(matrix way).circ as structural Verilog: 6 circuits, main circuit main
module main (
  input  [31:0] N,
  output [31:0] Nth
);

  wire \bit , clk, enable, enable2;
  wire [4:0] log_out;
  wire [31:0] bit_extender_1_out, calculator_out1, calculator_out2, calculator_out3, calculator_out4;

  enable_signal log (.in(N), .out(log_out));
  bit_provider bitprovider (.\input (N), .\bit (\bit ));
  calculate_logic calculator (
    .reset(1'b0), .enable(enable), .\bit (\bit ), .Out1(calculator_out1), .Out2(calculator_out2),
    .Out3(calculator_out3), .Out4(calculator_out4));
  // Probe on bit_extender_1_out
  assign bit_extender_1_out = {{27{1'b0}}, log_out};  // Bit_Extender bit_extender_1
  Clock clock_1 (.out(clk));
  counter_logic counter (.\input (bit_extender_1_out), .reset(1'b0), .enable(enable), .enable2(enable2));
  // Probe on calculator_out1
  // Probe on calculator_out2
  // Probe on calculator_out3
  // Probe on calculator_out4
  Multiplexer #(.width(32)) multiplexer_1 (
    .in0(calculator_out2), .in1({32{1'b0}}), .out(Nth), .sel(enable2));  // open: en
endmodule

module matrix_mult (
  input  [31:0] In1,
  input  [31:0] In2,
  input  [31:0] In3,
  input  [31:0] In4,
  input  [31:0] In5,
  input  [31:0] In6,
  input  [31:0] In7,
  input  [31:0] In8,
  output [31:0] Out1,
  output [31:0] Out2,
  output [31:0] Out3,
  output [31:0] Out4
);

  wire [31:0] multiplier_1_out, multiplier_2_out, multiplier_3_out, multiplier_4_out, multiplier_5_out,
       multiplier_6_out, multiplier_7_out, multiplier_8_out;

  Multiplier #(.width(32)) multiplier_1 (.a(In1), .b(In5), .out(multiplier_1_out));  // open: cin, cout
  Adder #(.width(32)) adder_1 (.a(multiplier_1_out), .b(multiplier_2_out), .out(Out1));  // open: cin, cout
  Multiplier #(.width(32)) multiplier_2 (.a(In2), .b(In7), .out(multiplier_2_out));  // open: cin, cout
  Multiplier #(.width(32)) multiplier_3 (.a(In1), .b(In6), .out(multiplier_3_out));  // open: cin, cout
  Adder #(.width(32)) adder_2 (.a(multiplier_3_out), .b(multiplier_4_out), .out(Out2));  // open: cin, cout
  Multiplier #(.width(32)) multiplier_4 (.a(In2), .b(In8), .out(multiplier_4_out));  // open: cin, cout
  Multiplier #(.width(32)) multiplier_5 (.a(In3), .b(In5), .out(multiplier_5_out));  // open: cin, cout
  Adder #(.width(32)) adder_3 (.a(multiplier_5_out), .b(multiplier_6_out), .out(Out3));  // open: cin, cout
  Multiplier #(.width(32)) multiplier_6 (.a(In4), .b(In7), .out(multiplier_6_out));  // open: cin, cout
  Multiplier #(.width(32)) multiplier_7 (.a(In3), .b(In6), .out(multiplier_7_out));  // open: cin, cout
  Adder #(.width(32)) adder_4 (.a(multiplier_7_out), .b(multiplier_8_out), .out(Out4));  // open: cin, cout
  Multiplier #(.width(32)) multiplier_8 (.a(In4), .b(In8), .out(multiplier_8_out));  // open: cin, cout
endmodule

module counter_logic (
  input  [31:0] \input ,
  input  reset,
  output enable,
  output enable2
);

  wire clk, comparator_1_lt;
  wire [31:0] adder_1_out, counter_1_q, subtractor_1_out;

  Clock clock_1 (.out(clk));
  Counter #(.width(32), .max('hffffffff)) counter_1 (
    .count(1'b1), .Q(counter_1_q), .clk(clk), .clr(reset));  // open: load, D, carry
  Subtractor #(.width(32)) subtractor_1 (.a(counter_1_q), .b(32'h1), .out(subtractor_1_out));  // open: bin, bout
  // Probe on subtractor_1_out
  // Probe on \input 
  Comparator #(.width(32)) comparator_1 (.a(\input ), .b(subtractor_1_out), .lt(comparator_1_lt));  // open: gt, eq
  not not_1 (enable, comparator_1_lt);
  Adder #(.width(32)) adder_1 (.a(\input ), .b(32'h4), .out(adder_1_out));  // open: cin, cout
  Comparator #(.width(32)) comparator_2 (.a(subtractor_1_out), .b(adder_1_out), .lt(enable2));  // open: gt, eq

  // Other names for the same wires on the sheet: max[31:0] = \input 
endmodule

module calculate_logic (
  input  reset,
  input  enable,
  input  \bit ,
  output [31:0] Out1,
  output [31:0] Out2,
  output [31:0] Out3,
  output [31:0] Out4
);

  wire clk, initialize;
  wire [31:0] M1_1in, M1_1out, M1_2in, M1_2out, M1_3in, M1_3out, M1_4in, M1_4out, M2_1in, M2_2in, M2_3in,
       M2_4in, matrix_mult_2_out1, matrix_mult_2_out2, matrix_mult_2_out3, matrix_mult_2_out4,
       multiplexer_1_out, multiplexer_2_out, multiplexer_3_out, multiplexer_4_out, multiplexer_5_out,
       multiplexer_6_out, multiplexer_7_out, multiplexer_8_out;

  Clock clock_1 (.out(clk));
  Counter #(.width(1), .max('h1), .ongoal("stay")) counter_1 (
    .Q(initialize), .clk(clk), .clr(reset));  // open: load, D, count, carry
  Multiplexer #(.width(32)) multiplexer_1 (
    .in0(32'h1), .in1(M1_1in), .out(multiplexer_1_out), .sel(initialize));  // open: en
  Multiplexer #(.width(32)) multiplexer_2 (
    .in0(32'h1), .in1(M1_2in), .out(multiplexer_2_out), .sel(initialize));  // open: en
  Multiplexer #(.width(32)) multiplexer_3 (
    .in0(32'h1), .in1(M1_3in), .out(multiplexer_3_out), .sel(initialize));  // open: en
  Multiplexer #(.width(32)) multiplexer_4 (
    .in0({32{1'b0}}), .in1(M1_4in), .out(multiplexer_4_out), .sel(initialize));  // open: en
  Register #(.width(32)) M1_1 (.D(multiplexer_1_out), .en(enable), .Q(M1_1out), .clk(clk), .clr(reset));
  Register #(.width(32)) M1_2 (.D(multiplexer_2_out), .en(enable), .Q(M1_2out), .clk(clk), .clr(reset));
  Register #(.width(32)) M1_3 (.D(multiplexer_3_out), .en(enable), .Q(M1_3out), .clk(clk), .clr(reset));
  Register #(.width(32)) M1_4 (.D(multiplexer_4_out), .en(enable), .Q(M1_4out), .clk(clk), .clr(reset));
  matrix_mult matrix_mult (
    .In1(M1_1out), .In2(M1_2out), .In3(M1_3out), .In4(M1_4out), .In5(M1_1out), .In6(M1_2out), .In7(M1_3out),
    .In8(M1_4out), .Out1(M1_1in), .Out2(M1_2in), .Out3(M1_3in), .Out4(M1_4in));
  Multiplexer #(.width(32)) multiplexer_5 (
    .in0(32'h1), .in1(M2_1in), .out(multiplexer_5_out), .sel(initialize));  // open: en
  Multiplexer #(.width(32)) multiplexer_6 (
    .in0({32{1'b0}}), .in1(M2_2in), .out(multiplexer_6_out), .sel(initialize));  // open: en
  Multiplexer #(.width(32)) multiplexer_7 (
    .in0({32{1'b0}}), .in1(M2_3in), .out(multiplexer_7_out), .sel(initialize));  // open: en
  Multiplexer #(.width(32)) multiplexer_8 (
    .in0(32'h1), .in1(M2_4in), .out(multiplexer_8_out), .sel(initialize));  // open: en
  Register #(.width(32)) M2_1 (.D(multiplexer_5_out), .en(enable), .Q(Out1), .clk(clk), .clr(reset));
  Register #(.width(32)) M2_2 (.D(multiplexer_6_out), .en(enable), .Q(Out2), .clk(clk), .clr(reset));
  Register #(.width(32)) M2_3 (.D(multiplexer_7_out), .en(enable), .Q(Out3), .clk(clk), .clr(reset));
  Register #(.width(32)) M2_4 (.D(multiplexer_8_out), .en(enable), .Q(Out4), .clk(clk), .clr(reset));
  matrix_mult matrix_mult_2 (
    .In1(M1_1out), .In2(M1_2out), .In3(M1_3out), .In4(M1_4out), .In5(Out1), .In6(Out2), .In7(Out3),
    .In8(Out4), .Out1(matrix_mult_2_out1), .Out2(matrix_mult_2_out2), .Out3(matrix_mult_2_out3),
    .Out4(matrix_mult_2_out4));
  Multiplexer #(.width(32)) multiplexer_9 (
    .in0(Out1), .in1(matrix_mult_2_out1), .out(M2_1in), .sel(\bit ));  // open: en
  Multiplexer #(.width(32)) multiplexer_10 (
    .in0(Out2), .in1(matrix_mult_2_out2), .out(M2_2in), .sel(\bit ));  // open: en
  Multiplexer #(.width(32)) multiplexer_11 (
    .in0(Out3), .in1(matrix_mult_2_out3), .out(M2_3in), .sel(\bit ));  // open: en
  Multiplexer #(.width(32)) multiplexer_12 (
    .in0(Out4), .in1(matrix_mult_2_out4), .out(M2_4in), .sel(\bit ));  // open: en

  // Other names for the same wires on the sheet: M2_1out[31:0] = Out1; M2_2out[31:0] = Out2; M2_3out[31:0] = Out3;
  //   M2_4out[31:0] = Out4
endmodule

module bit_provider (
  input  [31:0] \input ,
  output \bit 
);

  wire clock_1_out;
  wire [4:0] bit_extender_1_out, counter_1_q, subtractor_1_out;

  Counter #(.width(5), .max('h1f)) counter_1 (
    .count(1'b1), .Q(counter_1_q), .clk(clock_1_out));  // open: load, D, carry, clr
  Clock clock_1 (.out(clock_1_out));
  Multiplexer #(.select(5)) multiplexer_1 (
    .in0(\input [0]), .in1(\input [1]), .in2(\input [2]), .in3(\input [3]), .in4(\input [4]),
    .in5(\input [5]), .in6(\input [6]), .in7(\input [7]), .in8(\input [8]), .in9(\input [9]),
    .in10(\input [10]), .in11(\input [11]), .in12(\input [12]), .in13(\input [13]), .in14(\input [14]),
    .in15(\input [15]), .in16(\input [16]), .in17(\input [17]), .in18(\input [18]), .in19(\input [19]),
    .in20(\input [20]), .in21(\input [21]), .in22(\input [22]), .in23(\input [23]), .in24(\input [24]),
    .in25(\input [25]), .in26(\input [26]), .in27(\input [27]), .in28(\input [28]), .in29(\input [29]),
    .in30(\input [30]), .in31(\input [31]), .out(\bit ), .sel(subtractor_1_out));  // open: en
  assign bit_extender_1_out = {{4{1'b0}}, 1'b1};  // Bit_Extender bit_extender_1
  Subtractor #(.width(5)) subtractor_1 (
    .a(counter_1_q), .b(bit_extender_1_out), .out(subtractor_1_out));  // open: bin, bout
endmodule

module enable_signal (
  input  [31:0] in,
  output [4:0] out
);

  wire or_1_out;

  or or_1 (or_1_out, 1'b1, in[0]);
  Priority_Encoder #(.select(5)) priority_encoder_1 (
    .in0(or_1_out), .in1(in[1]), .in2(in[2]), .in3(in[3]), .in4(in[4]), .in5(in[5]), .in6(in[6]),
    .in7(in[7]), .in8(in[8]), .in9(in[9]), .in10(in[10]), .in11(in[11]), .in12(in[12]), .in13(in[13]),
    .in14(in[14]), .in15(in[15]), .in16(in[16]), .in17(in[17]), .in18(in[18]), .in19(in[19]), .in20(in[20]),
    .in21(in[21]), .in22(in[22]), .in23(in[23]), .in24(in[24]), .in25(in[25]), .in26(in[26]), .in27(in[27]),
    .in28(in[28]), .in29(in[29]), .in30(in[30]), .in31(in[31]), .out(out));  // open: gs, en_out, en_in
  // Probe on out
  Adder #(.width(5)) adder_1 (.b(5'b00001));  // open: a, out, cin, cout
endmodule
