// Logisim project Logisim_fibonacci(simple way).circ as structural Verilog: 3 circuits, main circuit main
module main (
  input  [2:0] N,
  output [3:0] Nth
);

  wire clock_1_out, comparator_1_gt;
  wire [7:0] time_counter_1_out_2;
  wire [7:4] fibonacci_adder_1_output;

  time_counter time_counter_1 (.clock(clock_1_out), .out_2(time_counter_1_out_2));
  Clock clock_1 (.out(clock_1_out));
  // Probe on time_counter_1_out_2
  Comparator comparator_1 (.a({{5{1'b0}}, N}), .b(time_counter_1_out_2), .gt(comparator_1_gt));  // open: eq, lt
  fibonacci_adder fibonacci_adder_1 (
    .\output ({fibonacci_adder_1_output, Nth}), .clock(clock_1_out), .enable(comparator_1_gt));
endmodule

module fibonacci_adder (
  input  clock,
  input  enable,
  output [7:0] \output 
);

  wire and_1_out, register_1_q;
  wire [7:0] adder_1_out, B_q, multiplexer_1_out, not_1_out;

  not not_1 (not_1_out[0], not_1_out[7]);
  Register A (.D(multiplexer_1_out), .en(not_1_out[0]), .Q(\output ), .clk(and_1_out));  // open: clr
  Register #(.width(1)) register_1 (
    .D(and_1_out), .en(not_1_out[0]), .Q(register_1_q), .clk(and_1_out), .clr(not_1_out[7]));
  Adder adder_1 (.a(\output ), .b(B_q), .out(adder_1_out), .cin(not_1_out[7]), .cout(not_1_out[7]));
  Register B (.D(\output ), .en(not_1_out[0]), .Q(B_q), .clk(and_1_out));  // open: clr
  and and_1 (and_1_out, clock, enable);
  Multiplexer #(.width(8)) multiplexer_1 (
    .in0({{7{not_1_out[7]}}, not_1_out[0]}), .in1(adder_1_out), .out(multiplexer_1_out), .sel(register_1_q),
    .en(not_1_out[0]));
endmodule

module time_counter (
  input  clock,
  output [7:0] out_2
);

  wire not_2_out, not_3_out, register_2_q;
  wire [0:0] not_1_out;
  wire [7:0] adder_1_out;

  not not_1 (not_1_out[0], 1'b0);
  Adder adder_1 (.a(out_2), .b({{7{1'b0}}, not_1_out[0]}), .out(adder_1_out));  // open: cin, cout
  Register register_1 (.D(adder_1_out), .en(not_1_out[0]), .Q(out_2), .clk(not_2_out), .clr(not_3_out));
  not not_2 (not_2_out, clock);
  not not_3 (not_3_out, register_2_q);
  Register #(.width(1)) register_2 (.D(clock), .en(not_1_out[0]), .Q(register_2_q), .clk(clock), .clr(1'b0));
endmodule
