// Logisim project Logisim_mod5(fake Moore FSM).circ as structural Verilog: 4 circuits, main circuit mod5
module mod5 (
  input  In,
  output s0,
  output s1,
  output s2,
  output s3,
  output s4
);

  wire [1:0] state_store_1_output, state_transition_1_out;

  state_transition state_transition_1 (.In(In), .In2(state_store_1_output), .out(state_transition_1_out));
  \output  output_1 (.In(state_transition_1_out), .s0(s0), .s1(s1), .s2(s2), .s3(s3), .s4(s4));
  state_store state_store_1 (.Input(state_transition_1_out), .Output(state_store_1_output));
endmodule

// 状态转移
module state_transition (
  input  In,
  input  [1:0] In2,
  output [1:0] out
);

  wire and_1_out, and_2_out, and_3_out, and_4_out, and_5_out, and_6_out, and_7_out, and_8_out, and_9_out,
       and_10_out, not_1_out, not_2_out, not_3_out, not_4_out, not_5_out, not_6_out, not_7_out, not_8_out,
       or_2_out, or_4_out;

  not not_1 (not_1_out, In2[0]);
  not not_2 (not_2_out, In2[1]);
  not not_3 (not_3_out, In);
  not not_4 (not_4_out, In2[0]);
  not not_5 (not_5_out, In);
  not not_6 (not_6_out, In2[0]);
  and and_1 (and_1_out, not_1_out, In2[1]);
  and and_2 (and_2_out, In2[0], not_2_out);
  and and_3 (and_3_out, not_3_out, not_4_out);
  and and_4 (and_4_out, not_5_out, In2[0]);
  not not_7 (not_7_out, In2[1]);
  and and_5 (and_5_out, In, not_6_out);
  not not_8 (not_8_out, In2[1]);
  and and_6 (and_6_out, In, In2[0]);
  or or_1 (out[0], and_1_out, and_2_out);
  and and_7 (and_7_out, and_3_out, In2[1]);
  and and_8 (and_8_out, and_4_out, not_7_out);
  and and_9 (and_9_out, and_5_out, not_8_out);
  and and_10 (and_10_out, and_6_out, In2[1]);
  or or_2 (or_2_out, and_7_out, and_8_out);
  or or_3 (out[1], or_2_out, or_4_out);
  or or_4 (or_4_out, and_9_out, and_10_out);
endmodule

// 状态存储
module state_store (
  input  [1:0] Input,
  output [1:0] Output
);

  wire clock_out, not_1_out;

  not not_1 (not_1_out, 1'b0);
  Clock clock (.out(clock_out));
  Register #(.width(2)) register_1 (.D(Input), .en(not_1_out), .Q(Output), .clk(clock_out));  // open: clr
endmodule

// 输出
module \output  (
  input  [1:0] In,
  output s0,
  output s1,
  output s2,
  output s3,
  output s4
);

  wire not_1_out, not_2_out, not_3_out, not_4_out;

  not not_1 (not_1_out, In[0]);
  not not_2 (not_2_out, In[1]);
  not not_3 (not_3_out, In[0]);
  not not_4 (not_4_out, In[1]);
  and and_1 (s4, In[0], In[1]);
  and and_2 (s1, not_1_out, not_2_out);
  and and_3 (s2, not_3_out, In[1]);
  and and_4 (s3, In[0], not_4_out);

  assign s0 = 1'b0;
endmodule
